// Logisim project dhw1.circ as structural Verilog: 6 circuits, main circuit TempMon
module TempMon (
  input  [2:0] TEMP_2_0,
  output [6:0] LEFT_6_0,
  output [6:0] RIGHT_6_0
);

  left Left_Display (
    .temp0(TEMP_2_0[2]), .temp1(TEMP_2_0[1]), .temp2(TEMP_2_0[0]), .lseg0(LEFT_6_0[0]), .lseg1(LEFT_6_0[1]),
    .lseg2(LEFT_6_0[2]), .lseg3(LEFT_6_0[3]), .lseg4(LEFT_6_0[4]), .lseg5(LEFT_6_0[5]), .lseg6(LEFT_6_0[6]));
  right Right_Display (
    .temp0(TEMP_2_0[2]), .temp1(TEMP_2_0[1]), .temp2(TEMP_2_0[0]), .rseg0(RIGHT_6_0[0]),
    .rseg1(RIGHT_6_0[1]), .rseg2(RIGHT_6_0[2]), .rseg3(RIGHT_6_0[3]), .rseg4(RIGHT_6_0[4]),
    .rseg5(RIGHT_6_0[5]), .rseg6(RIGHT_6_0[6]));
endmodule

module TestBench1 (
  input  [2:0] TEMP_2_0
);

  wire [6:0] tempmon_1_left_6_0, tempmon_1_right_6_0;

  TempMon tempmon_1 (.TEMP_2_0(TEMP_2_0), .LEFT_6_0(tempmon_1_left_6_0), .RIGHT_6_0(tempmon_1_right_6_0));
  _7_Segment_Display u_7_segment_display_1 (
    .g(tempmon_1_left_6_0[0]), .f(tempmon_1_left_6_0[1]), .a(tempmon_1_left_6_0[6]),
    .b(tempmon_1_left_6_0[5]), .e(tempmon_1_left_6_0[2]), .d(tempmon_1_left_6_0[3]), .c(tempmon_1_left_6_0[4]));  // open: dp
  _7_Segment_Display u_7_segment_display_2 (
    .g(tempmon_1_right_6_0[0]), .f(tempmon_1_right_6_0[1]), .a(tempmon_1_right_6_0[6]),
    .b(tempmon_1_right_6_0[5]), .e(tempmon_1_right_6_0[2]), .d(tempmon_1_right_6_0[3]),
    .c(tempmon_1_right_6_0[4]));  // open: dp
endmodule

module TempMonWithAlarm (
  input  [2:0] TEMP_2_0,
  input  [2:0] TEMPSETPOINT_2_0,
  output [6:0] RIGHT_6_0,
  output [6:0] LEFT_6_0,
  output TOOHOT
);

  wire comparator_1_eq, comparator_1_gt;

  TempMon tempmon_1 (.TEMP_2_0(TEMP_2_0), .LEFT_6_0(RIGHT_6_0), .RIGHT_6_0(LEFT_6_0));
  Comparator #(.width(3), .mode("unsigned")) comparator_1 (
    .a(TEMP_2_0), .b(TEMPSETPOINT_2_0), .gt(comparator_1_gt), .eq(comparator_1_eq));  // open: lt
  or or_1 (TOOHOT, comparator_1_gt, comparator_1_eq);
endmodule

module TestBench2 (
  input  [2:0] TEMP_2_0,
  input  [2:0] TEMPSETPOINT_2_0
);

  wire tempmonwithalarm_1_toohot;
  wire [6:0] tempmonwithalarm_1_left_6_0, tempmonwithalarm_1_right_6_0;

  _7_Segment_Display u_7_segment_display_1 (
    .g(tempmonwithalarm_1_right_6_0[0]), .f(tempmonwithalarm_1_right_6_0[1]),
    .a(tempmonwithalarm_1_right_6_0[6]), .b(tempmonwithalarm_1_right_6_0[5]),
    .e(tempmonwithalarm_1_right_6_0[2]), .d(tempmonwithalarm_1_right_6_0[3]),
    .c(tempmonwithalarm_1_right_6_0[4]));  // open: dp
  _7_Segment_Display u_7_segment_display_2 (
    .g(tempmonwithalarm_1_left_6_0[0]), .f(tempmonwithalarm_1_left_6_0[1]),
    .a(tempmonwithalarm_1_left_6_0[6]), .b(tempmonwithalarm_1_left_6_0[5]),
    .e(tempmonwithalarm_1_left_6_0[2]), .d(tempmonwithalarm_1_left_6_0[3]), .c(tempmonwithalarm_1_left_6_0[4]));  // open: dp
  TempMonWithAlarm tempmonwithalarm_1 (
    .TEMP_2_0(TEMP_2_0), .TEMPSETPOINT_2_0(TEMPSETPOINT_2_0), .RIGHT_6_0(tempmonwithalarm_1_right_6_0),
    .LEFT_6_0(tempmonwithalarm_1_left_6_0), .TOOHOT(tempmonwithalarm_1_toohot));
  LED led_1 (.in(tempmonwithalarm_1_toohot));
  // Simple_buzzer simple_buzzer_1: pin names not known; wires that end beside it: tempmonwithalarm_1_toohot
endmodule

module left (
  input  temp0,
  input  temp1,
  input  temp2,
  output lseg0,
  output lseg1,
  output lseg2,
  output lseg3,
  output lseg4,
  output lseg5,
  output lseg6
);

  wire nand_1_out, nand_2_out, nand_3_out, nand_4_out, nand_5_out, nand_6_out, nand_7_out, nand_8_out,
       nand_9_out, nand_10_out, nand_11_out, nand_12_out, nand_13_out, nand_14_out, nand_15_out, nand_17_out,
       nand_18_out, nand_19_out, nand_20_out, nand_22_out, nand_23_out, nand_24_out, nand_25_out,
       nand_26_out, nand_27_out, nand_28_out, nand_29_out, nand_30_out, nand_31_out, nand_32_out, nand_33_out;

  nand nand_1 (nand_1_out, temp0, temp0);
  nand nand_2 (nand_2_out, temp1, temp1);
  nand nand_3 (nand_3_out, temp2, temp2);
  nand nand_4 (nand_4_out, temp0, temp0);
  nand nand_5 (nand_5_out, temp1, temp1);
  nand nand_6 (nand_6_out, temp2, temp2);
  nand nand_7 (nand_7_out, temp2, temp2);
  nand nand_8 (nand_8_out, temp0, temp0);
  nand nand_9 (nand_9_out, temp1, temp1);
  nand nand_10 (nand_10_out, temp2, temp2);
  nand nand_11 (nand_11_out, temp2, temp2);
  nand nand_12 (nand_12_out, temp0, temp0);
  nand nand_13 (nand_13_out, temp1, temp1);
  nand nand_14 (nand_14_out, temp2, temp2);
  nand nand_15 (nand_15_out, temp2, temp2);
  nand nand_16 (lseg4, temp0, temp1, temp2);
  nand nand_17 (nand_17_out, temp0, temp0);
  nand nand_18 (nand_18_out, temp0, temp0);
  nand nand_19 (nand_19_out, temp1, temp1);
  nand nand_20 (nand_20_out, temp2, temp2);
  nand nand_21 (lseg6, temp0, temp1, temp2);
  nand nand_22 (nand_22_out, nand_1_out, nand_2_out, nand_3_out);
  nand nand_23 (nand_23_out, temp0, temp1);
  nand nand_24 (nand_24_out, nand_4_out, nand_5_out, nand_6_out);
  nand nand_25 (nand_25_out, temp0, temp1, nand_7_out);
  nand nand_26 (nand_26_out, nand_8_out, nand_9_out, nand_10_out);
  nand nand_27 (nand_27_out, temp0, temp1, nand_11_out);
  nand nand_28 (nand_28_out, nand_12_out, nand_13_out, nand_14_out);
  nand nand_29 (nand_29_out, temp0, temp1, nand_15_out);
  nand nand_30 (nand_30_out, nand_17_out, temp2);
  nand nand_31 (nand_31_out, nand_18_out, temp1);
  nand nand_32 (nand_32_out, temp0, nand_19_out);
  nand nand_33 (nand_33_out, temp0, nand_20_out);
  nand nand_34 (lseg0, nand_22_out, nand_23_out);
  nand nand_35 (lseg1, nand_24_out, nand_25_out);
  nand nand_36 (lseg2, nand_26_out, nand_27_out);
  nand nand_37 (lseg3, nand_28_out, nand_29_out);
  nand nand_38 (lseg5, nand_30_out, nand_31_out, nand_32_out, nand_33_out);
endmodule

module right (
  input  temp0,
  input  temp1,
  input  temp2,
  output rseg0,
  output rseg1,
  output rseg2,
  output rseg3,
  output rseg4,
  output rseg5,
  output rseg6
);

  wire nand_1_out, nand_2_out, nand_3_out, nand_4_out, nand_5_out, nand_8_out, nand_9_out, nand_10_out,
       nand_11_out, nand_13_out, nand_14_out, nand_15_out, nand_16_out, nand_17_out, nand_18_out,
       nand_19_out, nand_20_out, nand_21_out;

  nand nand_1 (nand_1_out, temp0, temp0);
  nand nand_2 (nand_2_out, temp2, temp2);
  nand nand_3 (nand_3_out, temp1, temp1);
  nand nand_4 (nand_4_out, temp0, temp0);
  nand nand_5 (nand_5_out, temp2, temp2);
  nand nand_6 (rseg2, temp1, temp2);
  nand nand_7 (rseg3, temp1, temp2);
  nand nand_8 (nand_8_out, temp0, temp0);
  nand nand_9 (nand_9_out, temp2, temp2);
  nand nand_10 (nand_10_out, temp1, temp1);
  nand nand_11 (nand_11_out, temp2, temp2);
  nand nand_12 (rseg6, temp1, temp2);
  nand nand_13 (nand_13_out, nand_1_out, nand_2_out);
  nand nand_14 (nand_14_out, temp1, temp2);
  nand nand_15 (nand_15_out, temp0, nand_3_out);
  nand nand_16 (nand_16_out, nand_4_out, temp2);
  nand nand_17 (nand_17_out, temp0, nand_5_out);
  nand nand_18 (nand_18_out, nand_8_out, temp2);
  nand nand_19 (nand_19_out, temp0, nand_9_out);
  nand nand_20 (nand_20_out, nand_10_out, temp2);
  nand nand_21 (nand_21_out, temp1, nand_11_out);
  nand nand_22 (rseg0, nand_13_out, nand_14_out, nand_15_out);
  nand nand_23 (rseg1, temp1, nand_16_out, nand_17_out);
  nand nand_24 (rseg4, temp1, nand_18_out, nand_19_out);
  nand nand_25 (rseg5, temp0, nand_20_out, nand_21_out);
endmodule
