// Logisim project libm16dhw3.circ as structural Verilog: 5 circuits, main circuit CALC
module CALC (
);

  wire button_2_out, button_3_out, button_4_out, button_5_out, button_6_out, button_7_out, button_8_out,
       button_9_out, button_10_out, button_11_out, button_12_out, button_13_out, button_out, clock_1_out,
       CLR_out, D, DEC_out, DEL_out, ENT_out, H, HEX_out, L, pwronrst_1_rst, RUN_out, S, TWC_out, U;
  wire [2:0] B0, B1, B2, B3, B4, MR1_out, MS1_out;
  wire [3:0] _0_out, T0, T1, T2, T3, T4;
  wire [5:0] _4_out;

  Clock clock_1 (.out(clock_1_out));
  Button _7 (.out(_4_out[3]));
  Button _4 (.out(_4_out[0]));
  Button _1 (.out(_0_out[1]));
  Button button (.out(button_out));
  PWRONRST pwronrst_1 (.CLK(clock_1_out), .RST(pwronrst_1_rst));
  Button _8 (.out(_4_out[4]));
  Button _5 (.out(_4_out[1]));
  Button _2 (.out(_0_out[2]));
  Button _0 (.out(_0_out[0]));
  Button _9 (.out(_4_out[5]));
  Button MS1 (.out(MS1_out[0]));
  Button CLR (.out(CLR_out));
  Button _6 (.out(_4_out[2]));
  Button _3 (.out(_0_out[3]));
  Button button_2 (.out(button_2_out));
  Button ENT (.out(ENT_out));
  Button button_3 (.out(button_3_out));
  _7_Segment_Display u_7_segment_display_1 (.g(S));  // open: f, a, b, e, d, c, dp
  LED led_1 (.in(D));
  LED led_2 (.in(H));
  LED led_3 (.in(U));
  Button MR1 (.out(MR1_out[0]));
  Button MS2 (.out(MS1_out[1]));
  Button DEC (.out(DEC_out));
  Button DEL (.out(DEL_out));
  Button button_4 (.out(button_4_out));
  Button button_5 (.out(button_5_out));
  Button button_6 (.out(button_6_out));
  Button button_7 (.out(button_7_out));
  _7_Segment_Display u_7_segment_display_2 (
    .g(T4[3]), .f(T4[2]), .a(T4[1]), .b(T4[0]), .e(B4[0]), .d(B4[1]), .c(B4[2]));  // open: dp
  _7_Segment_Display u_7_segment_display_3 (
    .g(T3[3]), .f(T3[2]), .a(T3[1]), .b(T3[0]), .e(B3[0]), .d(B3[1]), .c(B3[2]));  // open: dp
  Button MR2 (.out(MR1_out[1]));
  Button HEX (.out(HEX_out));
  Button button_8 (.out(button_8_out));
  Button button_9 (.out(button_9_out));
  _7_Segment_Display u_7_segment_display_4 (
    .g(T2[3]), .f(T2[2]), .a(T2[1]), .b(T2[0]), .e(B2[0]), .d(B2[1]), .c(B2[2]));  // open: dp
  _7_Segment_Display u_7_segment_display_5 (
    .g(T1[3]), .f(T1[2]), .a(T1[1]), .b(T1[0]), .e(B1[0]), .d(B1[1]), .c(B1[2]));  // open: dp
  Button MR3 (.out(MR1_out[2]));
  Button MS3 (.out(MS1_out[2]));
  Button TWC (.out(TWC_out));
  Button button_10 (.out(button_10_out));
  Button button_11 (.out(button_11_out));
  Button button_12 (.out(button_12_out));
  Button RUN (.out(RUN_out));
  Button button_13 (.out(button_13_out));
  _7_Segment_Display u_7_segment_display_6 (
    .g(T0[3]), .f(T0[2]), .a(T0[1]), .b(T0[0]), .e(B0[0]), .d(B0[1]), .c(B0[2]));  // open: dp
  LED led_4 (.in(L));
  CALC_CORE calc_core_1 (
    .CLK(clock_1_out), .RST(pwronrst_1_rst), .DIG({_4_out, _0_out}), .ADD(button_3_out), .SUB(button_7_out),
    .MUL(button_6_out), .DIV(button_9_out), .REM(button_13_out), .NEG(button_out), .INV(button_2_out),
    .AND(button_5_out), .OR(button_4_out), .XOR(button_8_out), .LSHFTL(button_11_out),
    .LSHFTR(button_12_out), .ASHFTR(button_10_out), .RUN(RUN_out), .ENT(ENT_out), .CLR(CLR_out),
    .DEL(DEL_out), .MS_2_0(MS1_out), .MR_2_0(MR1_out), .SGN(S), .SSD4({B4, T4}), .SSD3({B3, T3}),
    .SSD2({B2, T2}), .SSD1({B1, T1}), .SSD0({B0, T0}), .DECDISP(D), .HEXDISP(H), .TWCDISP(U), .DEC(DEC_out),
    .HEX(HEX_out), .TWC(TWC_out), .LED(L));

  // Notes on the sheet:
  //   RESET FOR FIRST CLOCK
  //   DEC
  //   HEX
  //   UNS
  //   M16 CALCULATOR
endmodule

module CALC_CORE (
  input  CLK,
  input  RST,
  input  [9:0] DIG,
  input  ADD,
  input  SUB,
  input  MUL,
  input  DIV,
  input  REM,
  input  NEG,
  input  INV,
  input  AND,
  input  OR,
  input  XOR,
  input  LSHFTL,
  input  LSHFTR,
  input  ASHFTR,
  input  RUN,
  input  ENT,
  input  CLR,
  input  DEL,
  input  [2:0] MS_2_0,
  input  [2:0] MR_2_0,
  input  DEC,
  input  HEX,
  input  TWC,
  output SGN,
  output LED,
  output DECDISP,
  output HEXDISP,
  output TWCDISP,
  output [6:0] SSD4,
  output [6:0] SSD3,
  output [6:0] SSD2,
  output [6:0] SSD1,
  output [6:0] SSD0
);
endmodule

module PWRONRST (
  input  CLK,
  output RST
);

  wire d_ff_1_q, nor_1_out, not_1_out;

  D_Flip_Flop d_ff_1 (.clk(CLK), .D(not_1_out), .Q(d_ff_1_q));  // open: Qn, preset, en, reset
  not not_1 (not_1_out, nor_1_out);
  nor nor_1 (nor_1_out, d_ff_1_q, RST);
  D_Flip_Flop d_ff_2 (.clk(CLK), .D(nor_1_out), .Q(RST));  // open: Qn, preset, en, reset

  // Notes on the sheet:
  //   This circuit sets RST=1 for one clock cycle at the beginning and then 0 afterwards.
endmodule

module Binary16toBCD5 (
  input  [15:0] IN,
  output SGN,
  output [3:0] OUT10K,
  output [3:0] OUT1K,
  output [3:0] OUT100,
  output [3:0] OUT10,
  output [3:0] OUT1
);

  wire C1_s0, C1_s1, C1_s2, C1_s3, C2_s0, C2_s1, C2_s2, C2_s3, C3_s0, C3_s1, C3_s2, C3_s3, C4_s0, C4_s1,
       C4_s2, C4_s3, C5_s0, C5_s1, C5_s2, C5_s3, C6_s0, C6_s1, C6_s2, C6_s3, C7_s0, C7_s1, C7_s2, C7_s3,
       C8_s0, C8_s1, C8_s2, C8_s3, C9_s0, C9_s1, C9_s2, C9_s3, C10_s0, C10_s1, C10_s2, C10_s3, C11_s0,
       C11_s1, C11_s2, C11_s3, C12_s0, C12_s1, C12_s2, C12_s3, C14_s0, C14_s1, C14_s2, C14_s3, C15_s0,
       C15_s1, C15_s2, C15_s3, C16_s0, C16_s1, C16_s2, C16_s3, C17_s0, C17_s1, C17_s2, C17_s3, C18_s0,
       C18_s1, C18_s2, C18_s3, C19_s0, C19_s1, C19_s2, C19_s3, C20_s0, C20_s1, C20_s2, C20_s3, C21_s0,
       C21_s1, C21_s2, C21_s3, C22_s0, C22_s1, C22_s2, C22_s3, C24_s0, C24_s1, C24_s2, C24_s3, C25_s0,
       C25_s1, C25_s2, C25_s3, C26_s0, C26_s1, C26_s2, C26_s3, C27_s0, C27_s1, C27_s2, C27_s3, C28_s0,
       C28_s1, C28_s2, C28_s3, C29_s0, C29_s1, C29_s2, C29_s3, C31_s0, C31_s1, C31_s2, C32_s0, C32_s1,
       C32_s2, C33_s0, C33_s1, C33_s2;
  wire [15:0] negator_1_out;
  wire [15:1] multiplexer_1_out;

  ADD3 C14 (.A3(1'b0), .A2(C1_s3), .S3(C14_s3), .A1(C2_s3), .A0(C3_s3), .S2(C14_s2), .S1(C14_s1), .S0(C14_s0));
  ADD3 C24 (.A3(1'b0), .A2(C14_s3), .S3(C24_s3), .A1(C15_s3), .A0(C16_s3), .S2(C24_s2), .S1(C24_s1), .S0(C24_s0));
  ADD3 C25 (.A3(C24_s2), .A2(C24_s1), .S3(C25_s3), .A1(C24_s0), .A0(C17_s3), .S2(C25_s2), .S1(C25_s1), .S0(C25_s0));
  ADD3 C31 (.A3(1'b0), .A2(C24_s3), .S3(OUT10K[3]), .A1(C25_s3), .A0(C26_s3), .S2(C31_s2), .S1(C31_s1), .S0(C31_s0));
  ADD3 C32 (.A3(C31_s2), .A2(C31_s1), .S3(OUT10K[2]), .A1(C31_s0), .A0(C27_s3), .S2(C32_s2), .S1(C32_s1), .S0(C32_s0));
  ADD3 C33 (.A3(C32_s2), .A2(C32_s1), .S3(OUT10K[1]), .A1(C32_s0), .A0(C28_s3), .S2(C33_s2), .S1(C33_s1), .S0(C33_s0));
  Multiplexer #(.width(16), .enable("false")) multiplexer_1 (
    .in0(IN), .in1(negator_1_out), .out({multiplexer_1_out, OUT1[0]}), .sel(IN[15]));
  Negator #(.width(16)) negator_1 (.in(IN), .out(negator_1_out));
  ADD3 C1 (
    .A3(1'b0), .A2(multiplexer_1_out[15]), .S3(C1_s3), .A1(multiplexer_1_out[14]),
    .A0(multiplexer_1_out[13]), .S2(C1_s2), .S1(C1_s1), .S0(C1_s0));
  ADD3 C2 (
    .A3(C1_s2), .A2(C1_s1), .S3(C2_s3), .A1(C1_s0), .A0(multiplexer_1_out[12]), .S2(C2_s2), .S1(C2_s1),
    .S0(C2_s0));
  ADD3 C3 (
    .A3(C2_s2), .A2(C2_s1), .S3(C3_s3), .A1(C2_s0), .A0(multiplexer_1_out[11]), .S2(C3_s2), .S1(C3_s1),
    .S0(C3_s0));
  ADD3 C4 (
    .A3(C3_s2), .A2(C3_s1), .S3(C4_s3), .A1(C3_s0), .A0(multiplexer_1_out[10]), .S2(C4_s2), .S1(C4_s1),
    .S0(C4_s0));
  ADD3 C15 (.A3(C14_s2), .A2(C14_s1), .S3(C15_s3), .A1(C14_s0), .A0(C4_s3), .S2(C15_s2), .S1(C15_s1), .S0(C15_s0));
  ADD3 C16 (.A3(C15_s2), .A2(C15_s1), .S3(C16_s3), .A1(C15_s0), .A0(C5_s3), .S2(C16_s2), .S1(C16_s1), .S0(C16_s0));
  ADD3 C17 (.A3(C16_s2), .A2(C16_s1), .S3(C17_s3), .A1(C16_s0), .A0(C6_s3), .S2(C17_s2), .S1(C17_s1), .S0(C17_s0));
  ADD3 C18 (.A3(C17_s2), .A2(C17_s1), .S3(C18_s3), .A1(C17_s0), .A0(C7_s3), .S2(C18_s2), .S1(C18_s1), .S0(C18_s0));
  ADD3 C26 (.A3(C25_s2), .A2(C25_s1), .S3(C26_s3), .A1(C25_s0), .A0(C18_s3), .S2(C26_s2), .S1(C26_s1), .S0(C26_s0));
  ADD3 C27 (.A3(C26_s2), .A2(C26_s1), .S3(C27_s3), .A1(C26_s0), .A0(C19_s3), .S2(C27_s2), .S1(C27_s1), .S0(C27_s0));
  ADD3 C28 (.A3(C27_s2), .A2(C27_s1), .S3(C28_s3), .A1(C27_s0), .A0(C20_s3), .S2(C28_s2), .S1(C28_s1), .S0(C28_s0));
  ADD3 C29 (.A3(C28_s2), .A2(C28_s1), .S3(C29_s3), .A1(C28_s0), .A0(C21_s3), .S2(C29_s2), .S1(C29_s1), .S0(C29_s0));
  ADD3 C34 (
    .A3(C33_s2), .A2(C33_s1), .S3(OUT10K[0]), .A1(C33_s0), .A0(C29_s3), .S2(OUT1K[3]), .S1(OUT1K[2]),
    .S0(OUT1K[1]));
  ADD3 C5 (
    .A3(C4_s2), .A2(C4_s1), .S3(C5_s3), .A1(C4_s0), .A0(multiplexer_1_out[9]), .S2(C5_s2), .S1(C5_s1),
    .S0(C5_s0));
  ADD3 C6 (
    .A3(C5_s2), .A2(C5_s1), .S3(C6_s3), .A1(C5_s0), .A0(multiplexer_1_out[8]), .S2(C6_s2), .S1(C6_s1),
    .S0(C6_s0));
  ADD3 C7 (
    .A3(C6_s2), .A2(C6_s1), .S3(C7_s3), .A1(C6_s0), .A0(multiplexer_1_out[7]), .S2(C7_s2), .S1(C7_s1),
    .S0(C7_s0));
  ADD3 C8 (
    .A3(C7_s2), .A2(C7_s1), .S3(C8_s3), .A1(C7_s0), .A0(multiplexer_1_out[6]), .S2(C8_s2), .S1(C8_s1),
    .S0(C8_s0));
  ADD3 C19 (.A3(C18_s2), .A2(C18_s1), .S3(C19_s3), .A1(C18_s0), .A0(C8_s3), .S2(C19_s2), .S1(C19_s1), .S0(C19_s0));
  ADD3 C20 (.A3(C19_s2), .A2(C19_s1), .S3(C20_s3), .A1(C19_s0), .A0(C9_s3), .S2(C20_s2), .S1(C20_s1), .S0(C20_s0));
  ADD3 C21 (.A3(C20_s2), .A2(C20_s1), .S3(C21_s3), .A1(C20_s0), .A0(C10_s3), .S2(C21_s2), .S1(C21_s1), .S0(C21_s0));
  ADD3 C22 (.A3(C21_s2), .A2(C21_s1), .S3(C22_s3), .A1(C21_s0), .A0(C11_s3), .S2(C22_s2), .S1(C22_s1), .S0(C22_s0));
  ADD3 C30 (
    .A3(C29_s2), .A2(C29_s1), .S3(OUT1K[0]), .A1(C29_s0), .A0(C22_s3), .S2(OUT100[3]), .S1(OUT100[2]),
    .S0(OUT100[1]));
  ADD3 C9 (
    .A3(C8_s2), .A2(C8_s1), .S3(C9_s3), .A1(C8_s0), .A0(multiplexer_1_out[5]), .S2(C9_s2), .S1(C9_s1),
    .S0(C9_s0));
  ADD3 C10 (
    .A3(C9_s2), .A2(C9_s1), .S3(C10_s3), .A1(C9_s0), .A0(multiplexer_1_out[4]), .S2(C10_s2), .S1(C10_s1),
    .S0(C10_s0));
  ADD3 C11 (
    .A3(C10_s2), .A2(C10_s1), .S3(C11_s3), .A1(C10_s0), .A0(multiplexer_1_out[3]), .S2(C11_s2), .S1(C11_s1),
    .S0(C11_s0));
  ADD3 C12 (
    .A3(C11_s2), .A2(C11_s1), .S3(C12_s3), .A1(C11_s0), .A0(multiplexer_1_out[2]), .S2(C12_s2), .S1(C12_s1),
    .S0(C12_s0));
  ADD3 C23 (
    .A3(C22_s2), .A2(C22_s1), .S3(OUT100[0]), .A1(C22_s0), .A0(C12_s3), .S2(OUT10[3]), .S1(OUT10[2]),
    .S0(OUT10[1]));
  ADD3 C13 (
    .A3(C12_s2), .A2(C12_s1), .S3(OUT10[0]), .A1(C12_s0), .A0(multiplexer_1_out[1]), .S2(OUT1[3]),
    .S1(OUT1[2]), .S0(OUT1[1]));

  assign SGN = IN[15];
endmodule

module ADD3 (
  input  A3,
  input  A2,
  input  A1,
  input  A0,
  output S3,
  output S2,
  output S1,
  output S0
);

  wire and_1_out, and_2_out, and_3_out, and_4_out, and_5_out, and_6_out, and_7_out, and_8_out, and_9_out,
       and_10_out, and_11_out, and_12_out, and_13_out, not_1_out, not_2_out, not_3_out, not_4_out, not_5_out,
       not_6_out, not_7_out, not_8_out;

  and and_1 (and_1_out, A2, A0);
  and and_2 (and_2_out, A2, A1);
  and and_3 (and_3_out, A2, not_1_out, not_2_out);
  not not_1 (not_1_out, A1);
  not not_2 (not_2_out, A0);
  and and_4 (and_4_out, A3, A0);
  and and_5 (and_5_out, A3, A1);
  not not_3 (not_3_out, A2);
  and and_6 (and_6_out, not_3_out, A1);
  and and_7 (and_7_out, A1, A0);
  and and_8 (and_8_out, A3, not_4_out);
  not not_4 (not_4_out, A0);
  and and_9 (and_9_out, A3, A2);
  not not_5 (not_5_out, A3);
  and and_10 (and_10_out, not_5_out, not_6_out, A0);
  not not_6 (not_6_out, A2);
  and and_11 (and_11_out, A2, A1, not_7_out);
  not not_7 (not_7_out, A0);
  and and_12 (and_12_out, A3, not_8_out);
  not not_8 (not_8_out, A0);
  and and_13 (and_13_out, A3, A1);
  or or_1 (S3, and_1_out, and_2_out, A3);
  or or_2 (S2, and_3_out, and_4_out, and_5_out);
  or or_3 (S1, and_6_out, and_7_out, and_8_out, and_9_out);
  or or_4 (S0, and_10_out, and_11_out, and_12_out, and_13_out);
endmodule
