// Logisim project dhw2.circ as structural Verilog: 18 circuits, main circuit TESTBENCH_DP
module ALU (
  input  [15:0] DINA,
  input  [15:0] DINB,
  input  [3:0] OPCODE,
  output [15:0] DOUT,
  output FZER,
  output FNEG,
  output FOVF
);

  wire and_1_out, and_2_out, and_3_out, and_4_out, decoder_1_out4, decoder_1_out5, decoder_1_out6,
       decoder_1_out7, op5_1_out_3, op6_1_out_4, op7_1_out_4, op8_1_out_4, xnor_1_out, xnor_2_out,
       xnor_3_out, xnor_4_out, xnor_5_out, xnor_6_out, xnor_7_out, xnor_8_out, xnor_9_out, xnor_10_out,
       xnor_11_out, xnor_12_out, xnor_13_out, xnor_14_out, xnor_15_out, xnor_16_out;
  wire [15:0] op1, op2, op3, op4, op5, op6, op7, op8, op9, op10, op11;

  Decoder #(.select(4)) decoder_1 (
    .out4(decoder_1_out4), .out5(decoder_1_out5), .out6(decoder_1_out6), .out7(decoder_1_out7), .sel(OPCODE));  // open: out0, out1, out2, out3, out8, out9, out10, out11, out12, out13, out14, out15, en
  op1 op1_1 (.in_1(DINA), .out_2(op1));
  op2 op2_1 (.in_1(DINA), .in_2(DINB), .out_3(op2));
  op3 op3_1 (.in_1(DINA), .in_2(DINB), .out_3(op3));
  op4 op4_1 (.in_1(DINA), .in_2(DINB), .out_3(op4));
  op5 op5_1 (.in_1(DINB), .out_2(op5), .out_3(op5_1_out_3));
  op6 op6_1 (.in_1(DINA), .in_2(DINB), .out_3(op6), .out_4(op6_1_out_4));
  op7 op7_1 (.in_1(DINA), .in_2(DINB), .out_3(op7), .out_4(op7_1_out_4));
  op8 op8_1 (.in_1(DINA), .in_2(DINB), .out_3(op8), .out_4(op8_1_out_4));
  op9 op9_1 (.in_1(DINA), .in_2(DINB), .out_3(op9));
  op10 op10_1 (.in_1(DINA), .in_2(DINB), .out_3(op10));
  op11 op11_1 (.in_1(DINA), .in_2(DINB), .out_3(op11));
  and and_1 (and_1_out, decoder_1_out4, op5_1_out_3);
  and and_2 (and_2_out, decoder_1_out5, op6_1_out_4);
  and and_3 (and_3_out, decoder_1_out6, op7_1_out_4);
  and and_4 (and_4_out, decoder_1_out7, op8_1_out_4);
  Multiplexer #(.select(4), .width(16)) multiplexer_1 (
    .in0(op1), .in1(op2), .in2(op3), .in3(op4), .in4(op5), .in5(op6), .in6(op7), .in7(op8), .in8(op9),
    .in9(op10), .in10(op11), .in11({16{1'b0}}), .in14({16{1'b0}}), .in15({16{1'b0}}), .out(DOUT), .sel(OPCODE));  // open: in12, in13, en
  or or_1 (FOVF, and_1_out, and_2_out, and_3_out, and_4_out);
  xnor xnor_1 (xnor_1_out, 1'b0, DOUT[5]);
  xnor xnor_2 (xnor_2_out, 1'b0, DOUT[6]);
  xnor xnor_3 (xnor_3_out, 1'b0, DOUT[7]);
  xnor xnor_4 (xnor_4_out, DOUT[8], 1'b0);
  xnor xnor_5 (xnor_5_out, DOUT[9], 1'b0);
  xnor xnor_6 (xnor_6_out, DOUT[10], 1'b0);
  xnor xnor_7 (xnor_7_out, DOUT[11], 1'b0);
  xnor xnor_8 (xnor_8_out, 1'b0, DOUT[0]);
  xnor xnor_9 (xnor_9_out, 1'b0, DOUT[1]);
  xnor xnor_10 (xnor_10_out, 1'b0, DOUT[2]);
  xnor xnor_11 (xnor_11_out, 1'b0, DOUT[3]);
  xnor xnor_12 (xnor_12_out, 1'b0, DOUT[4]);
  xnor xnor_13 (xnor_13_out, DOUT[12], 1'b0);
  xnor xnor_14 (xnor_14_out, DOUT[13], 1'b0);
  xnor xnor_15 (xnor_15_out, DOUT[14], 1'b0);
  xnor xnor_16 (xnor_16_out, DOUT[15], 1'b0);
  and and_5 (FZER, xnor_8_out, xnor_9_out, xnor_10_out, xnor_11_out, xnor_12_out, xnor_1_out, xnor_2_out, xnor_3_out, xnor_4_out, xnor_5_out, xnor_6_out, xnor_7_out, xnor_13_out, xnor_14_out, xnor_15_out, xnor_16_out);

  assign FNEG = DOUT[15];

  // Other names for the same wires on the sheet: ZERO = FZER
endmodule

module REG (
  input  [15:0] DINA,
  input  [3:0] SELOUTA,
  input  [3:0] SELOUTB,
  input  [3:0] SELIN,
  input  WR,
  input  CLK,
  output [15:0] DOUTA,
  output [15:0] DOUTB
);

  wire and_1_out, and_2_out, and_3_out, and_4_out, and_5_out, and_6_out, and_7_out, and_8_out, and_9_out,
       and_10_out, and_11_out, and_12_out, and_13_out, and_14_out, decoder_1_out1, decoder_1_out2,
       decoder_1_out3, decoder_1_out4, decoder_1_out5, decoder_1_out6, decoder_1_out7, decoder_1_out8,
       decoder_1_out9, decoder_1_out10, decoder_1_out11, decoder_1_out12, decoder_1_out13, decoder_1_out14;
  wire [15:0] _1, _2, _3, _4, _5, _6, _7, _8, _9, A, B, C, D, E;

  Multiplexer #(.select(4), .width(16)) multiplexer_1 (
    .in0(16'h1), .in1(_1), .in2(_2), .in3(_3), .in4(_4), .in5(_5), .in6(_6), .in7(_7), .in8(_8), .in9(_9),
    .in10(A), .in11(B), .in12(C), .in13(D), .in14(E), .out(DOUTB), .sel(SELOUTB));  // open: in15, en
  Multiplexer #(.select(4), .width(16)) multiplexer_2 (
    .in0({16{1'b0}}), .in1(_1), .in2(_2), .in3(_3), .in4(_4), .in5(_5), .in6(_6), .in7(_7), .in8(_8),
    .in9(_9), .in10(A), .in11(B), .in12(C), .in13(D), .in14(E), .out(DOUTA), .sel(SELOUTA));  // open: in15, en
  Decoder #(.select(4)) decoder_1 (
    .out1(decoder_1_out1), .out2(decoder_1_out2), .out3(decoder_1_out3), .out4(decoder_1_out4),
    .out5(decoder_1_out5), .out6(decoder_1_out6), .out7(decoder_1_out7), .out8(decoder_1_out8),
    .out9(decoder_1_out9), .out10(decoder_1_out10), .out11(decoder_1_out11), .out12(decoder_1_out12),
    .out13(decoder_1_out13), .out14(decoder_1_out14), .sel(SELIN));  // open: out0, out15, en
  and and_1 (and_1_out, decoder_1_out1, WR);
  and and_2 (and_2_out, decoder_1_out4, WR);
  and and_3 (and_3_out, decoder_1_out7, WR);
  and and_4 (and_4_out, decoder_1_out10, WR);
  and and_5 (and_5_out, decoder_1_out13, WR);
  Register #(.width(16)) register_1 (.D(DINA), .en(and_1_out), .Q(_1), .clk(CLK));  // open: clr
  Register #(.width(16)) register_2 (.D(DINA), .en(and_2_out), .Q(_4), .clk(CLK));  // open: clr
  Register #(.width(16)) register_3 (.D(DINA), .en(and_3_out), .Q(_7), .clk(CLK));  // open: clr
  Register #(.width(16)) register_4 (.D(DINA), .en(and_4_out), .Q(A), .clk(CLK));  // open: clr
  Register #(.width(16)) register_5 (.D(DINA), .en(and_5_out), .Q(D), .clk(CLK));  // open: clr
  and and_6 (and_6_out, decoder_1_out2, WR);
  and and_7 (and_7_out, decoder_1_out5, WR);
  and and_8 (and_8_out, decoder_1_out8, WR);
  and and_9 (and_9_out, decoder_1_out11, WR);
  and and_10 (and_10_out, decoder_1_out14, WR);
  Register #(.width(16)) register_6 (.D(DINA), .en(and_6_out), .Q(_2), .clk(CLK));  // open: clr
  Register #(.width(16)) register_7 (.D(DINA), .en(and_7_out), .Q(_5), .clk(CLK));  // open: clr
  Register #(.width(16)) register_8 (.D(DINA), .en(and_8_out), .Q(_8), .clk(CLK));  // open: clr
  Register #(.width(16)) register_9 (.D(DINA), .en(and_9_out), .Q(B), .clk(CLK));  // open: clr
  Register #(.width(16)) register_10 (.D(DINA), .en(and_10_out), .Q(E), .clk(CLK));  // open: clr
  and and_11 (and_11_out, decoder_1_out3, WR);
  and and_12 (and_12_out, decoder_1_out6, WR);
  and and_13 (and_13_out, decoder_1_out9, WR);
  and and_14 (and_14_out, decoder_1_out12, WR);
  Register #(.width(16)) register_11 (.D(DINA), .en(and_11_out), .Q(_3), .clk(CLK));  // open: clr
  Register #(.width(16)) register_12 (.D(DINA), .en(and_12_out), .Q(_6), .clk(CLK));  // open: clr
  Register #(.width(16)) register_13 (.D(DINA), .en(and_13_out), .Q(_9), .clk(CLK));  // open: clr
  Register #(.width(16)) register_14 (.D(DINA), .en(and_14_out), .Q(C), .clk(CLK));  // open: clr

  // Other names for the same wires on the sheet: a_t[3:0] = SELOUTA; b_t[3:0] = SELOUTB; data[15:0] = DINA;
  //   in[3:0] = SELIN
endmodule

module DATAPATH (
  input  [15:0] DIN,
  input  [15:0] INSTR,
  input  CLK,
  output [15:0] DOUT,
  output FZERO,
  output FNEG,
  output FOVF
);

  wire decoder_1_out12, decoder_1_out13, decoder_1_out14, decoder_1_out15, decoder_2_out0, decoder_2_out1,
       decoder_2_out2, decoder_2_out3, decoder_2_out4, decoder_2_out5, decoder_2_out6, decoder_2_out7,
       decoder_2_out8, decoder_2_out9, decoder_2_out10, decoder_2_out11, decoder_2_out12, decoder_2_out13,
       decoder_2_out14, decoder_2_out15, nor_1_out, or_1_out;
  wire [3:0] outstoreaddress;
  wire [15:0] multiplexer_1_out, multiplexer_2_out, multiplexer_3_out, reg_1_douta, reg_1_doutb;

  Decoder #(.select(4)) decoder_1 (
    .out12(decoder_1_out12), .out13(decoder_1_out13), .out14(decoder_1_out14), .out15(decoder_1_out15),
    .sel(INSTR[15:12]));  // open: out0, out1, out2, out3, out4, out5, out6, out7, out8, out9, out10, out11, en
  Multiplexer #(.width(16)) multiplexer_1 (.in0(DOUT), .in1(DIN), .out(multiplexer_1_out), .sel(or_1_out));  // open: en
  nor nor_1 (nor_1_out, decoder_1_out12, decoder_1_out13, decoder_1_out14, decoder_1_out15);
  REG reg_1 (
    .DINA(multiplexer_1_out), .SELOUTA(INSTR[11:8]), .SELOUTB(INSTR[7:4]), .SELIN(outstoreaddress),
    .WR(nor_1_out), .CLK(CLK), .DOUTA(reg_1_douta), .DOUTB(reg_1_doutb));
  or or_1 (or_1_out, decoder_2_out15, decoder_2_out0);
  Decoder #(.select(4)) decoder_2 (
    .out0(decoder_2_out0), .out1(decoder_2_out1), .out2(decoder_2_out2), .out3(decoder_2_out3),
    .out4(decoder_2_out4), .out5(decoder_2_out5), .out6(decoder_2_out6), .out7(decoder_2_out7),
    .out8(decoder_2_out8), .out9(decoder_2_out9), .out10(decoder_2_out10), .out11(decoder_2_out11),
    .out12(decoder_2_out12), .out13(decoder_2_out13), .out14(decoder_2_out14), .out15(decoder_2_out15),
    .sel(INSTR[3:0]));  // open: en
  Multiplexer #(.select(4), .width(16)) multiplexer_2 (
    .in0({16{1'b0}}), .in1(reg_1_douta), .in2(reg_1_douta), .in3(reg_1_douta), .in4(reg_1_douta),
    .in5(reg_1_douta), .in6(reg_1_douta), .in7(reg_1_douta), .in8(reg_1_douta), .in9(reg_1_douta),
    .in10(reg_1_douta), .in11(reg_1_douta), .in12(reg_1_douta), .in13(reg_1_douta), .in14(reg_1_douta),
    .in15(DIN), .out(multiplexer_2_out), .sel(INSTR[11:8]));  // open: en
  Multiplexer #(.select(4), .width(16)) multiplexer_3 (
    .in0(16'h1), .in1(reg_1_doutb), .in2(reg_1_doutb), .in3(reg_1_doutb), .in4(reg_1_doutb),
    .in5(reg_1_doutb), .in6(reg_1_doutb), .in7(reg_1_doutb), .in8(reg_1_doutb), .in9(reg_1_doutb),
    .in10(reg_1_doutb), .in11(reg_1_doutb), .in12(reg_1_doutb), .in13(reg_1_doutb), .in14(reg_1_doutb),
    .in15(DIN), .out(multiplexer_3_out), .sel(INSTR[7:4]));  // open: en
  Priority_Encoder #(.select(4)) priority_encoder_1 (
    .in0(decoder_2_out0), .in1(decoder_2_out1), .in2(decoder_2_out2), .in3(decoder_2_out3),
    .in4(decoder_2_out4), .in5(decoder_2_out5), .in6(decoder_2_out6), .in7(decoder_2_out7),
    .in8(decoder_2_out8), .in9(decoder_2_out9), .in10(decoder_2_out10), .in11(decoder_2_out11),
    .in12(decoder_2_out12), .in13(decoder_2_out13), .in14(decoder_2_out14), .in15(decoder_2_out15),
    .out(outstoreaddress));  // open: gs, en_out, en_in
  ALU alu_1 (
    .DINA(multiplexer_2_out), .DINB(multiplexer_3_out), .OPCODE(INSTR[15:12]), .DOUT(DOUT), .FZER(FZERO),
    .FNEG(FNEG), .FOVF(FOVF));

  // Other names for the same wires on the sheet: _7_4[3:0] = INSTR[7:4]; _11_8[3:0] = INSTR[11:8];
  //   fstoreout[3:0] = INSTR[3:0]; opcode[3:0] = INSTR[15:12]
endmodule

module TESTBENCH_DP (
  input  [15:0] DIN_15_0,
  input  [15:0] INSTR_15_0
);

  wire CLK_out, datapath_1_fneg, datapath_1_fovf, datapath_1_fzero;
  wire [15:0] out;

  Hex_Digit_Display hex_digit_display_1 (.value(DIN_15_0[15:12]));  // open: dp
  Hex_Digit_Display hex_digit_display_2 (.value(DIN_15_0[7:4]));  // open: dp
  Hex_Digit_Display hex_digit_display_3 (.value(DIN_15_0[11:8]));  // open: dp
  Clock CLK (.out(CLK_out));
  Hex_Digit_Display hex_digit_display_4 (.value(out[15:12]));  // open: dp
  Hex_Digit_Display hex_digit_display_5 (.value(DIN_15_0[3:0]));  // open: dp
  DATAPATH datapath_1 (
    .DIN(DIN_15_0), .INSTR(INSTR_15_0), .CLK(CLK_out), .DOUT(out), .FZERO(datapath_1_fzero),
    .FNEG(datapath_1_fneg), .FOVF(datapath_1_fovf));
  Hex_Digit_Display hex_digit_display_6 (.value(out[7:4]));  // open: dp
  Hex_Digit_Display hex_digit_display_7 (.value(out[11:8]));  // open: dp
  Hex_Digit_Display hex_digit_display_8 (.value(INSTR_15_0[15:12]));  // open: dp
  Hex_Digit_Display hex_digit_display_9 (.value(out[3:0]));  // open: dp
  Hex_Digit_Display hex_digit_display_10 (.value(INSTR_15_0[11:8]));  // open: dp
  LED FZER (.in(datapath_1_fzero));
  LED FNEG (.in(datapath_1_fneg));
  LED FOVF (.in(datapath_1_fovf));
  Hex_Digit_Display hex_digit_display_11 (.value(INSTR_15_0[7:4]));  // open: dp
  Hex_Digit_Display hex_digit_display_12 (.value(INSTR_15_0[3:0]));  // open: dp

  // Other names for the same wires on the sheet: IN[15:0] = DIN_15_0; OP[15:0] = INSTR_15_0
endmodule

module op1 (
  input  [15:0] in_1,
  output [15:0] out_2
);

  assign out_2 = ~in_1;  // NOT_Gate not_1, 16 bits wide

  // Notes on the sheet:
  //   invert
endmodule

module op2 (
  input  [15:0] in_1,
  input  [15:0] in_2,
  output [15:0] out_3
);

  assign out_3 = in_1 & in_2;  // AND_Gate and_1, 16 bits wide

  // Notes on the sheet:
  //   and
endmodule

module op3 (
  input  [15:0] in_1,
  input  [15:0] in_2,
  output [15:0] out_3
);

  assign out_3 = in_1 | in_2;  // OR_Gate or_1, 16 bits wide

  // Notes on the sheet:
  //   OR
endmodule

module op4 (
  input  [15:0] in_1,
  input  [15:0] in_2,
  output [15:0] out_3
);

  assign out_3 = in_1 ^ in_2;  // XOR_Gate xor_1, 16 bits wide

  // Notes on the sheet:
  //   xor
endmodule

module op5 (
  input  [15:0] in_1,
  output [15:0] out_2,
  output out_3
);

  wire [15:0] not_1_out;

  assign not_1_out = ~in_1;  // NOT_Gate not_1, 16 bits wide
  Adder #(.width(16)) adder_1 (.a(not_1_out), .b(16'h1), .out(out_2), .cout(out_3));  // open: cin

  // Notes on the sheet:
  //   negative
endmodule

module op6 (
  input  [15:0] in_1,
  input  [15:0] in_2,
  output [15:0] out_3,
  output out_4
);

  and and_1 (out_3[15], in_2[15], in_1[15]);
  Adder #(.width(15)) adder_1 (.a(in_1[14:0]), .b(in_2[14:0]), .out(out_3[14:0]), .cout(out_4));  // open: cin

  // Notes on the sheet:
  //   adder
  //   only gives the correct sign for positive positive or negative negative addition
endmodule

module op7 (
  input  [15:0] in_1,
  input  [15:0] in_2,
  output [15:0] out_3,
  output out_4
);

  Subtractor #(.width(15)) subtractor_1 (.a(in_1[14:0]), .b(in_2[14:0]), .out(out_3[14:0]), .bout(out_4));  // open: bin

  assign out_3[15] = 1'b0;

  // Notes on the sheet:
  //   subtrapt
endmodule

module op8 (
  input  [15:0] in_1,
  input  [15:0] in_2,
  output [15:0] out_3,
  output out_4
);

  wire [14:0] multiplier_1_cout;

  Multiplier #(.width(15)) multiplier_1 (
    .a(in_1[14:0]), .b(in_2[14:0]), .out(out_3[14:0]), .cout(multiplier_1_cout));  // open: cin
  xor xor_1 (out_3[15], in_1[15], in_2[15]);
  or or_1 (out_4, multiplier_1_cout[14], multiplier_1_cout[13], multiplier_1_cout[12], multiplier_1_cout[11], multiplier_1_cout[10], multiplier_1_cout[9], multiplier_1_cout[8], multiplier_1_cout[7], multiplier_1_cout[6], multiplier_1_cout[5], multiplier_1_cout[4], multiplier_1_cout[3], multiplier_1_cout[2], multiplier_1_cout[1], multiplier_1_cout[0]);

  // Notes on the sheet:
  //   multiplier
endmodule

module op9 (
  input  [15:0] in_1,
  input  [15:0] in_2,
  output [15:0] out_3
);

  Shifter #(.width(16)) shifter_1 (.in(in_1), .\dist (in_2[3:0]), .out(out_3));

  // Notes on the sheet:
  //   leftnshifter
endmodule

module op10 (
  input  [15:0] in_1,
  input  [15:0] in_2,
  output [15:0] out_3
);

  Shifter #(.width(16), .shift("lr")) shifter_1 (.in(in_1), .\dist (in_2[3:0]), .out(out_3));

  // Notes on the sheet:
  //   lshift right
endmodule

module op11 (
  input  [15:0] in_1,
  input  [15:0] in_2,
  output [15:0] out_3
);

  Shifter #(.width(16), .shift("ar")) shifter_1 (.in(in_1), .\dist (in_2[3:0]), .out(out_3));

  // Notes on the sheet:
  //   ashifter
endmodule

module REGOLD (
  input  [15:0] DINA,
  input  [3:0] SELOUTA,
  input  [3:0] SELOUTB,
  input  [3:0] SELIN_3_0,
  input  WR,
  input  CLK,
  output [15:0] DOUTA,
  output [15:0] DOUTB
);

  wire and_1_out, and_2_out, and_3_out, and_4_out, and_5_out, and_6_out, and_7_out, and_8_out, and_9_out,
       and_10_out, and_11_out, and_12_out, and_13_out, and_14_out, decoder_1_out1, decoder_1_out2,
       decoder_1_out3, decoder_1_out4, decoder_1_out5, decoder_1_out6, decoder_1_out7, decoder_1_out8,
       decoder_1_out9, decoder_1_out10, decoder_1_out11, decoder_1_out12, decoder_1_out13, decoder_1_out14;
  wire [15:0] register_1_q, register_2_q, register_3_q, register_4_q, register_5_q, register_6_q,
       register_7_q, register_8_q, register_9_q, register_10_q, register_11_q, register_12_q, register_13_q,
       register_14_q;

  Decoder #(.select(4)) decoder_1 (
    .out1(decoder_1_out1), .out2(decoder_1_out2), .out3(decoder_1_out3), .out4(decoder_1_out4),
    .out5(decoder_1_out5), .out6(decoder_1_out6), .out7(decoder_1_out7), .out8(decoder_1_out8),
    .out9(decoder_1_out9), .out10(decoder_1_out10), .out11(decoder_1_out11), .out12(decoder_1_out12),
    .out13(decoder_1_out13), .out14(decoder_1_out14), .sel(SELIN_3_0));  // open: out0, out15, en
  and and_1 (and_1_out, decoder_1_out1, CLK);
  and and_2 (and_2_out, decoder_1_out2, CLK);
  and and_3 (and_3_out, decoder_1_out3, CLK);
  and and_4 (and_4_out, decoder_1_out4, CLK);
  and and_5 (and_5_out, decoder_1_out5, CLK);
  and and_6 (and_6_out, decoder_1_out6, CLK);
  and and_7 (and_7_out, decoder_1_out7, CLK);
  and and_8 (and_8_out, decoder_1_out8, CLK);
  and and_9 (and_9_out, decoder_1_out9, CLK);
  and and_10 (and_10_out, decoder_1_out10, CLK);
  and and_11 (and_11_out, decoder_1_out11, CLK);
  and and_12 (and_12_out, decoder_1_out12, CLK);
  and and_13 (and_13_out, decoder_1_out13, CLK);
  and and_14 (and_14_out, decoder_1_out14, CLK);
  Register #(.width(16)) register_1 (.D(DINA), .en(WR), .Q(register_1_q), .clk(and_1_out));  // open: clr
  Register #(.width(16)) register_2 (.D(DINA), .en(WR), .Q(register_2_q), .clk(and_2_out));  // open: clr
  Register #(.width(16)) register_3 (.D(DINA), .en(WR), .Q(register_3_q), .clk(and_3_out));  // open: clr
  Register #(.width(16)) register_4 (.D(DINA), .en(WR), .Q(register_4_q), .clk(and_4_out));  // open: clr
  Register #(.width(16)) register_5 (.D(DINA), .en(WR), .Q(register_5_q), .clk(and_5_out));  // open: clr
  Register #(.width(16)) register_6 (.D(DINA), .en(WR), .Q(register_6_q), .clk(and_6_out));  // open: clr
  Register #(.width(16)) register_7 (.D(DINA), .en(WR), .Q(register_7_q), .clk(and_7_out));  // open: clr
  Register #(.width(16)) register_8 (.D(DINA), .en(WR), .Q(register_8_q), .clk(and_8_out));  // open: clr
  Register #(.width(16)) register_9 (.D(DINA), .en(WR), .Q(register_9_q), .clk(and_9_out));  // open: clr
  Register #(.width(16)) register_10 (.D(DINA), .en(WR), .Q(register_10_q), .clk(and_10_out));  // open: clr
  Register #(.width(16)) register_11 (.D(DINA), .en(WR), .Q(register_11_q), .clk(and_11_out));  // open: clr
  Register #(.width(16)) register_12 (.D(DINA), .en(WR), .Q(register_12_q), .clk(and_12_out));  // open: clr
  Register #(.width(16)) register_13 (.D(DINA), .en(WR), .Q(register_13_q), .clk(and_13_out));  // open: clr
  Register #(.width(16)) register_14 (.D(DINA), .en(WR), .Q(register_14_q), .clk(and_14_out));  // open: clr
  Multiplexer #(.select(4), .width(16)) multiplexer_1 (
    .in0({16{1'b0}}), .in1(register_1_q), .in2(register_2_q), .in3(register_3_q), .in4(register_4_q),
    .in5(register_5_q), .in6(register_6_q), .in7(register_7_q), .in8(register_8_q), .in9(register_9_q),
    .in10(register_10_q), .in11(register_11_q), .in12(register_12_q), .in13(register_13_q),
    .in14(register_14_q), .in15(DINA), .out(DOUTA), .sel(SELOUTA));  // open: en
  Multiplexer #(.select(4), .width(16)) multiplexer_2 (
    .in0({16{1'b0}}), .in1(register_1_q), .in2(register_2_q), .in3(register_3_q), .in4(register_4_q),
    .in5(register_5_q), .in6(register_6_q), .in7(register_7_q), .in8(register_8_q), .in9(register_9_q),
    .in10(register_10_q), .in11(register_11_q), .in12(register_12_q), .in13(register_13_q),
    .in14(register_14_q), .in15(DINA), .out(DOUTB), .sel(SELOUTB));  // open: en

  // Other names for the same wires on the sheet: a[3:0] = SELOUTA; b[3:0] = SELOUTB
endmodule

module DATAPATHOLD (
  input  [15:0] in_1,
  input  [3:0] in_2,
  input  [15:0] DIN_15_0,
  input  [15:0] in_4,
  input  [15:0] INSTR_15_0,
  input  CLK,
  output [15:0] DOUT_15_0,
  output FZER,
  output FNEG,
  output FOVF
);

  wire alu_1_fneg, alu_1_fovf, alu_1_fzer, and_1_out, decoder_1_out0, decoder_1_out1, decoder_1_out2,
       decoder_1_out3, decoder_1_out4, decoder_1_out5, decoder_1_out6, decoder_1_out7, decoder_1_out8,
       decoder_1_out9, decoder_1_out10, decoder_2_out0, decoder_2_out15, or_1_out;
  wire [15:0] alu_1_dout, multiplexer_1_out, regold_1_douta, regold_1_doutb;

  Decoder #(.select(4)) decoder_1 (
    .out0(decoder_1_out0), .out1(decoder_1_out1), .out2(decoder_1_out2), .out3(decoder_1_out3),
    .out4(decoder_1_out4), .out5(decoder_1_out5), .out6(decoder_1_out6), .out7(decoder_1_out7),
    .out8(decoder_1_out8), .out9(decoder_1_out9), .out10(decoder_1_out10), .sel(INSTR_15_0[15:12]));  // open: out11, out12, out13, out14, out15, en
  or or_1 (or_1_out, decoder_1_out0, decoder_1_out1, decoder_1_out2, decoder_1_out3, decoder_1_out4, decoder_1_out5, decoder_1_out6, decoder_1_out7, decoder_1_out8, decoder_1_out9, decoder_1_out10);
  D_Flip_Flop d_ff_1 ();  // open: clk, D, Q, Qn, preset, en, reset
  ALU alu_1 (
    .DINA(in_1), .DINB(in_4), .OPCODE(in_2), .DOUT(alu_1_dout), .FZER(alu_1_fzer), .FNEG(alu_1_fneg),
    .FOVF(alu_1_fovf));
  Decoder #(.select(4)) decoder_2 (
    .out0(decoder_2_out0), .out15(decoder_2_out15), .sel({4{INSTR_15_0[3]}}));  // open: out1, out2, out3, out4, out5, out6, out7, out8, out9, out10, out11, out12, out13, out14, en
  Multiplexer #(.width(16)) multiplexer_1 (
    .in0(DIN_15_0), .in1(DOUT_15_0), .out(multiplexer_1_out), .sel(and_1_out));  // open: en
  REGOLD regold_1 (
    .DINA(multiplexer_1_out), .SELOUTA(INSTR_15_0[11:8]), .SELOUTB(INSTR_15_0[7:4]), .WR(or_1_out),
    .CLK(CLK), .DOUTA(regold_1_douta), .DOUTB(regold_1_doutb));  // open: SELIN_3_0
  and and_1 (and_1_out, decoder_2_out0, decoder_2_out15);
  ALU alu_2 (
    .DINA(regold_1_douta), .DINB(regold_1_doutb), .OPCODE(INSTR_15_0[15:12]), .DOUT(DOUT_15_0), .FZER(FZER),
    .FNEG(FNEG), .FOVF(FOVF));

  assign INSTR_15_0[2:0] = {3{INSTR_15_0[3]}};

  // Other names for the same wires on the sheet: OPCODE[3:0] = INSTR_15_0[15:12]
endmodule

module qq (
);

  wire [14:0] adder_2_out;
  wire [15:15] adder_1_out;

  Adder #(.width(1)) adder_1 (.out(adder_1_out[15]));  // open: a, b, cin, cout
  Adder #(.width(15)) adder_2 (.out(adder_2_out));  // open: a, b, cin, cout
endmodule
