// Logisim project dhw3.circ as structural Verilog: 28 circuits, main circuit CALC
module CALC (
);

  wire button_2_out, button_3_out, button_4_out, button_5_out, button_6_out, button_7_out, button_8_out,
       button_9_out, button_10_out, button_11_out, button_12_out, button_13_out, button_out,
       calc_core_1_postop, clock_1_out, CLR_out, D, DEC_out, DEL_out, ENT_out, H, HEX_out, L, pwronrst_1_rst,
       RUN_out, S, TWC_out, U;
  wire [2:0] B0, B1, B2, B3, B4, MR1_out, MS1_out;
  wire [3:0] _0_out, T0, T1, T2, T3, T4;
  wire [5:0] _4_out;

  Clock clock_1 (.out(clock_1_out));
  Button _7 (.out(_4_out[3]));
  Button _4 (.out(_4_out[0]));
  Button _1 (.out(_0_out[1]));
  Button button (.out(button_out));
  PWRONRST pwronrst_1 (.CLK(clock_1_out), .RST(pwronrst_1_rst));
  Button _8 (.out(_4_out[4]));
  Button _5 (.out(_4_out[1]));
  Button _2 (.out(_0_out[2]));
  Button _0 (.out(_0_out[0]));
  Button _9 (.out(_4_out[5]));
  Button MS1 (.out(MS1_out[0]));
  Button _6 (.out(_4_out[2]));
  Button CLR (.out(CLR_out));
  Button _3 (.out(_0_out[3]));
  Button button_2 (.out(button_2_out));
  Button button_3 (.out(button_3_out));
  Button ENT (.out(ENT_out));
  _7_Segment_Display u_7_segment_display_1 (.g(S));  // open: f, a, b, e, d, c, dp
  LED led_1 (.in(D));
  LED led_2 (.in(H));
  LED led_3 (.in(U));
  Button MR1 (.out(MR1_out[0]));
  Button MS2 (.out(MS1_out[1]));
  Button DEC (.out(DEC_out));
  Button DEL (.out(DEL_out));
  Button button_4 (.out(button_4_out));
  Button button_5 (.out(button_5_out));
  Button button_6 (.out(button_6_out));
  Button button_7 (.out(button_7_out));
  _7_Segment_Display u_7_segment_display_2 (
    .g(T4[3]), .f(T4[2]), .a(T4[1]), .b(T4[0]), .e(B4[0]), .d(B4[1]), .c(B4[2]));  // open: dp
  _7_Segment_Display u_7_segment_display_3 (
    .g(T3[3]), .f(T3[2]), .a(T3[1]), .b(T3[0]), .e(B3[0]), .d(B3[1]), .c(B3[2]));  // open: dp
  Button MR2 (.out(MR1_out[1]));
  Button HEX (.out(HEX_out));
  Button button_8 (.out(button_8_out));
  Button button_9 (.out(button_9_out));
  _7_Segment_Display u_7_segment_display_4 (
    .g(T2[3]), .f(T2[2]), .a(T2[1]), .b(T2[0]), .e(B2[0]), .d(B2[1]), .c(B2[2]));  // open: dp
  _7_Segment_Display u_7_segment_display_5 (
    .g(T1[3]), .f(T1[2]), .a(T1[1]), .b(T1[0]), .e(B1[0]), .d(B1[1]), .c(B1[2]));  // open: dp
  Button MR3 (.out(MR1_out[2]));
  Button MS3 (.out(MS1_out[2]));
  Button button_10 (.out(button_10_out));
  Button TWC (.out(TWC_out));
  Button button_11 (.out(button_11_out));
  Button button_12 (.out(button_12_out));
  Button RUN (.out(RUN_out));
  Button button_13 (.out(button_13_out));
  _7_Segment_Display u_7_segment_display_6 (
    .g(T0[3]), .f(T0[2]), .a(T0[1]), .b(T0[0]), .e(B0[0]), .d(B0[1]), .c(B0[2]));  // open: dp
  LED led_4 (.in(L));
  CALC_CORE calc_core_1 (
    .CLK(clock_1_out), .RST(pwronrst_1_rst), .DIG({_4_out, _0_out}), .ADD(button_3_out), .SUB(button_7_out),
    .MUL(button_6_out), .DIV(button_9_out), .REM(button_13_out), .NEG(button_out), .INV(button_2_out),
    .AND(button_5_out), .OR(button_4_out), .XOR(button_8_out), .LSHFTL(button_12_out),
    .LSHFTR(button_11_out), .ASHFTR(button_10_out), .RUN(RUN_out), .ENT(ENT_out), .CLR(CLR_out),
    .DEL(DEL_out), .MS_2_0(MS1_out), .MR_2_0(MR1_out), .SGN(S), .SSD4({B4, T4}), .SSD3({B3, T3}),
    .SSD2({B2, T2}), .SSD1({B1, T1}), .SSD0({B0, T0}), .DECDISP(D), .HEXDISP(H), .TWCDISP(U), .DEC(DEC_out),
    .HEX(HEX_out), .TWC(TWC_out), .LED(L), .postop(calc_core_1_postop));

  // Notes on the sheet:
  //   RESET FOR FIRST CLOCK
  //   DEC
  //   HEX
  //   UNS
  //   M16 CALCULATOR
endmodule

module CALC_CORE (
  input  CLK,
  input  RST,
  input  [9:0] DIG,
  input  ADD,
  input  SUB,
  input  MUL,
  input  DIV,
  input  REM,
  input  NEG,
  input  INV,
  input  AND,
  input  OR,
  input  XOR,
  input  LSHFTL,
  input  LSHFTR,
  input  ASHFTR,
  input  RUN,
  input  ENT,
  input  CLR,
  input  DEL,
  input  [2:0] MS_2_0,
  input  [2:0] MR_2_0,
  input  DEC,
  input  HEX,
  input  TWC,
  output SGN,
  output LED,
  output DECDISP,
  output HEXDISP,
  output TWCDISP,
  output [6:0] SSD4,
  output [6:0] SSD3,
  output [6:0] SSD2,
  output [6:0] SSD1,
  output [6:0] SSD0,
  output postop
);

  wire _2B, and_1_out, and_3_out, clickonehigh_6_ispressed, clickonehigh_16_ispressed,
       clickonehigh_18_ispressed, clickonehigh_21_ispressed, clickstorerecallbuttonprocessor_1_amsr,
       clickstorerecallbuttonprocessor_2_amsr, clicktoggleforminusbutton_1_out_4, CLR_t, clrError,
       countpressed_1_err, d, DEC_t, DEL_t, eh, Error, HEX_t, n00_lastnumberenteredfromdigitbuttons_1_ovf,
       n01_datapathcontroller_1_opmode, n01_datapathcontroller_1_srmode, nand_1_out, nand_2_out, OP, OPOVER,
       or_4_out, or_5_out, or_6_out, or_7_out, or_9_out, or_10_out, or_11_out, OVF, TWC_t;
  wire [1:0] n11_1_displaymode_1_out_6, R, S;
  wire [2:0] C;
  wire [3:0] A, ctp, OPCODE;
  wire [3:1] B;
  wire [15:0] clickvalueofdigitclicked_1_out_3, n00_lastnumberenteredfromdigitbuttons_1_out_8,
       n01_datapathcontroller_1_out_8;

  ClickValueOfDigitClicked clickvalueofdigitclicked_1 (
    .Clicked_Operation(DIG), .CLK(CLK), .out_3(clickvalueofdigitclicked_1_out_3), .clickhappens(d));
  ClickOneHigh clickonehigh_1 (.press(ADD), .CLK(CLK), .ispressed(B[1]));
  ClickOneHigh clickonehigh_2 (.press(SUB), .CLK(CLK), .ispressed(B[2]));
  ClickOneHigh clickonehigh_3 (.press(MUL), .CLK(CLK), .ispressed(B[3]));
  ClickOneHigh clickonehigh_4 (.press(DIV), .CLK(CLK));  // open: ispressed
  ClickOneHigh clickonehigh_5 (.press(REM), .CLK(CLK));  // open: ispressed
  ClickOneHigh clickonehigh_6 (.press(NEG), .CLK(CLK), .ispressed(clickonehigh_6_ispressed));
  ClickOneHigh clickonehigh_7 (.press(INV), .CLK(CLK), .ispressed(A[0]));
  ClickOneHigh clickonehigh_8 (.press(AND), .CLK(CLK), .ispressed(A[1]));
  ClickOneHigh clickonehigh_9 (.press(OR), .CLK(CLK), .ispressed(A[2]));
  ClickOneHigh clickonehigh_10 (.press(XOR), .CLK(CLK), .ispressed(A[3]));
  ClickOneHigh clickonehigh_11 (.press(LSHFTL), .CLK(CLK), .ispressed(C[0]));
  ClickOneHigh clickonehigh_12 (.press(LSHFTR), .CLK(CLK), .ispressed(C[1]));
  ClickOneHigh clickonehigh_13 (.press(ASHFTR), .CLK(CLK), .ispressed(C[2]));
  ClickOneHigh clickonehigh_14 (.press(RUN), .CLK(CLK));  // open: ispressed
  ClickOneHigh clickonehigh_15 (.press(ENT), .CLK(CLK));  // open: ispressed
  ClickOneHigh clickonehigh_16 (.press(CLR), .CLK(CLK), .ispressed(clickonehigh_16_ispressed));
  ClickOneHigh clickonehigh_17 (.press(DEL), .CLK(CLK), .ispressed(DEL_t));
  ClickStoreRecallButtonProcessor clickstorerecallbuttonprocessor_1 (
    .in_1(MS_2_0), .CLK(CLK), .out_4(S), .amsr(clickstorerecallbuttonprocessor_1_amsr), .stopsr(or_4_out));
  ClickStoreRecallButtonProcessor clickstorerecallbuttonprocessor_2 (
    .in_1(MR_2_0), .CLK(CLK), .out_4(R), .amsr(clickstorerecallbuttonprocessor_2_amsr), .stopsr(or_5_out));
  ClickOneHigh clickonehigh_18 (.press(DEC), .CLK(CLK), .ispressed(clickonehigh_18_ispressed));
  ClickOneHigh clickonehigh_19 (.press(HEX), .CLK(CLK), .ispressed(HEX_t));
  ClickOneHigh clickonehigh_20 (.press(TWC), .CLK(CLK), .ispressed(TWC_t));
  ClickOneHigh clickonehigh_21 (.press(clickonehigh_6_ispressed), .CLK(CLK), .ispressed(clickonehigh_21_ispressed));
  ClickToggleForMinusButton clicktoggleforminusbutton_1 (
    .in_1(clickonehigh_21_ispressed), .CLK(CLK), .in_3(CLR_t), .out_4(clicktoggleforminusbutton_1_out_4));
  or or_1 (DEC_t, RST, clickonehigh_16_ispressed, clickonehigh_18_ispressed);
  or or_2 (CLR_t, eh, clickonehigh_16_ispressed);
  ClickOperation clickoperation_1 (
    .Clicked_Operation({{5{1'b0}}, C, B, 1'b0, A}), .CLK(CLK), .OPCODE(OPCODE), .clickhappens(OP));
  or or_3 (postop, OPOVER, OP, d);
  or or_4 (or_4_out, clickstorerecallbuttonprocessor_2_amsr, eh, postop);
  or or_5 (or_5_out, postop, eh, clickstorerecallbuttonprocessor_1_amsr);
  _00_LastNumberEnteredFromDigitButtons u_00_lastnumberenteredfromdigitbuttons_1 (
    .pressed(clickvalueofdigitclicked_1_out_3), .clickhappens(d), .cPressed(ctp), .CLR(CLR_t), .DEL(DEL_t),
    .NEG(clicktoggleforminusbutton_1_out_4), .CLK(CLK),
    .out_8(n00_lastnumberenteredfromdigitbuttons_1_out_8), .OVF(n00_lastnumberenteredfromdigitbuttons_1_ovf));
  CountPressed countpressed_1 (
    .numberpressed(d), .deletepressed(DEL_t), .cError(clrError), .CLK(CLK), .amountpressed(ctp),
    .ERR(countpressed_1_err));
  or or_6 (or_6_out, R[0], R[1]);
  or or_7 (or_7_out, S[0], S[1]);
  or or_8 (Error, OVF, n00_lastnumberenteredfromdigitbuttons_1_ovf, countpressed_1_err, _2B);
  or or_9 (or_9_out, OP, DEC_t, d);
  _01_DataPathController u_01_datapathcontroller_1 (
    .in_1(n00_lastnumberenteredfromdigitbuttons_1_out_8), .trueopcode(OPCODE), .recallwhere(R),
    .storewhere(S), .d(d), .in_6(CLR_t), .CLK(CLK), .out_8(n01_datapathcontroller_1_out_8),
    .OPmode(n01_datapathcontroller_1_opmode), .SRmode(n01_datapathcontroller_1_srmode), .out_11(OVF));
  or or_10 (or_10_out, d, n01_datapathcontroller_1_srmode);
  and and_1 (and_1_out, or_10_out, n01_datapathcontroller_1_opmode);
  CheckTooBig checktoobig_1 (.in_1(n01_datapathcontroller_1_out_8), .error(_2B));
  Decoder #(.select(2)) decoder_1 (
    .out0(DECDISP), .out1(HEXDISP), .out2(TWCDISP), .sel(n11_1_displaymode_1_out_6));  // open: out3, en
  _11_1_DisplayMode u_11_1_displaymode_1 (
    .DEC(or_9_out), .HEX(HEX_t), .TWC(TWC_t), .ERROR(Error), .CLK(CLK), .out_6(n11_1_displaymode_1_out_6));
  or or_11 (or_11_out, or_6_out, and_1_out, or_7_out);
  or or_12 (OPOVER, DEC_t, HEX_t, TWC_t, CLR_t, 1'b0);
  and and_2 (eh, or_11_out, d);
  DisplayMain displaymain_1 (
    .IN(n01_datapathcontroller_1_out_8), .DisplayMode(n11_1_displaymode_1_out_6), .SGN(SGN), .SSD4(SSD4),
    .SSD3(SSD3), .SSD2(SSD2), .SSD1(SSD1), .SSD0(SSD0));
  or or_13 (clrError, CLR_t, and_3_out);
  and and_3 (and_3_out, Error, OPOVER);
  nand nand_1 (nand_1_out, SSD4[0], SSD4[1], SSD4[2]);
  nand nand_2 (nand_2_out, SSD4[4], SSD4[5], SSD4[6]);
  // OR_Gate or_14 has open pins: in0=nand_1_out, in1=SSD4[3], in2=nand_2_out, out=open

  assign LED = 1'b0;
endmodule

module PWRONRST (
  input  CLK,
  output RST
);

  wire d_ff_1_q, nor_1_out, not_1_out;

  D_Flip_Flop d_ff_1 (.clk(CLK), .D(not_1_out), .Q(d_ff_1_q));  // open: Qn, preset, en, reset
  not not_1 (not_1_out, nor_1_out);
  nor nor_1 (nor_1_out, d_ff_1_q, RST);
  D_Flip_Flop d_ff_2 (.clk(CLK), .D(nor_1_out), .Q(RST));  // open: Qn, preset, en, reset

  // Notes on the sheet:
  //   This circuit sets RST=1 for one clock cycle at the beginning and then 0 afterwards.
endmodule

module Binary16toBCD5 (
  input  [15:0] IN,
  output SGN,
  output [3:0] OUT10K,
  output [3:0] OUT1K,
  output [3:0] OUT100,
  output [3:0] OUT10,
  output [3:0] OUT1
);

  wire C1_s0, C1_s1, C1_s2, C1_s3, C2_s0, C2_s1, C2_s2, C2_s3, C3_s0, C3_s1, C3_s2, C3_s3, C4_s0, C4_s1,
       C4_s2, C4_s3, C5_s0, C5_s1, C5_s2, C5_s3, C6_s0, C6_s1, C6_s2, C6_s3, C7_s0, C7_s1, C7_s2, C7_s3,
       C8_s0, C8_s1, C8_s2, C8_s3, C9_s0, C9_s1, C9_s2, C9_s3, C10_s0, C10_s1, C10_s2, C10_s3, C11_s0,
       C11_s1, C11_s2, C11_s3, C12_s0, C12_s1, C12_s2, C12_s3, C14_s0, C14_s1, C14_s2, C14_s3, C15_s0,
       C15_s1, C15_s2, C15_s3, C16_s0, C16_s1, C16_s2, C16_s3, C17_s0, C17_s1, C17_s2, C17_s3, C18_s0,
       C18_s1, C18_s2, C18_s3, C19_s0, C19_s1, C19_s2, C19_s3, C20_s0, C20_s1, C20_s2, C20_s3, C21_s0,
       C21_s1, C21_s2, C21_s3, C22_s0, C22_s1, C22_s2, C22_s3, C24_s0, C24_s1, C24_s2, C24_s3, C25_s0,
       C25_s1, C25_s2, C25_s3, C26_s0, C26_s1, C26_s2, C26_s3, C27_s0, C27_s1, C27_s2, C27_s3, C28_s0,
       C28_s1, C28_s2, C28_s3, C29_s0, C29_s1, C29_s2, C29_s3, C31_s0, C31_s1, C31_s2, C32_s0, C32_s1,
       C32_s2, C33_s0, C33_s1, C33_s2;
  wire [15:0] negator_1_out;
  wire [15:1] multiplexer_1_out;

  ADD3 C14 (.A3(1'b0), .A2(C1_s3), .S3(C14_s3), .A1(C2_s3), .A0(C3_s3), .S2(C14_s2), .S1(C14_s1), .S0(C14_s0));
  ADD3 C24 (.A3(1'b0), .A2(C14_s3), .S3(C24_s3), .A1(C15_s3), .A0(C16_s3), .S2(C24_s2), .S1(C24_s1), .S0(C24_s0));
  ADD3 C25 (.A3(C24_s2), .A2(C24_s1), .S3(C25_s3), .A1(C24_s0), .A0(C17_s3), .S2(C25_s2), .S1(C25_s1), .S0(C25_s0));
  ADD3 C31 (.A3(1'b0), .A2(C24_s3), .S3(OUT10K[3]), .A1(C25_s3), .A0(C26_s3), .S2(C31_s2), .S1(C31_s1), .S0(C31_s0));
  ADD3 C32 (.A3(C31_s2), .A2(C31_s1), .S3(OUT10K[2]), .A1(C31_s0), .A0(C27_s3), .S2(C32_s2), .S1(C32_s1), .S0(C32_s0));
  ADD3 C33 (.A3(C32_s2), .A2(C32_s1), .S3(OUT10K[1]), .A1(C32_s0), .A0(C28_s3), .S2(C33_s2), .S1(C33_s1), .S0(C33_s0));
  Multiplexer #(.width(16), .enable("false")) multiplexer_1 (
    .in0(IN), .in1(negator_1_out), .out({multiplexer_1_out, OUT1[0]}), .sel(IN[15]));
  Negator #(.width(16)) negator_1 (.in(IN), .out(negator_1_out));
  ADD3 C1 (
    .A3(1'b0), .A2(multiplexer_1_out[15]), .S3(C1_s3), .A1(multiplexer_1_out[14]),
    .A0(multiplexer_1_out[13]), .S2(C1_s2), .S1(C1_s1), .S0(C1_s0));
  ADD3 C2 (
    .A3(C1_s2), .A2(C1_s1), .S3(C2_s3), .A1(C1_s0), .A0(multiplexer_1_out[12]), .S2(C2_s2), .S1(C2_s1),
    .S0(C2_s0));
  ADD3 C3 (
    .A3(C2_s2), .A2(C2_s1), .S3(C3_s3), .A1(C2_s0), .A0(multiplexer_1_out[11]), .S2(C3_s2), .S1(C3_s1),
    .S0(C3_s0));
  ADD3 C4 (
    .A3(C3_s2), .A2(C3_s1), .S3(C4_s3), .A1(C3_s0), .A0(multiplexer_1_out[10]), .S2(C4_s2), .S1(C4_s1),
    .S0(C4_s0));
  ADD3 C15 (.A3(C14_s2), .A2(C14_s1), .S3(C15_s3), .A1(C14_s0), .A0(C4_s3), .S2(C15_s2), .S1(C15_s1), .S0(C15_s0));
  ADD3 C16 (.A3(C15_s2), .A2(C15_s1), .S3(C16_s3), .A1(C15_s0), .A0(C5_s3), .S2(C16_s2), .S1(C16_s1), .S0(C16_s0));
  ADD3 C17 (.A3(C16_s2), .A2(C16_s1), .S3(C17_s3), .A1(C16_s0), .A0(C6_s3), .S2(C17_s2), .S1(C17_s1), .S0(C17_s0));
  ADD3 C18 (.A3(C17_s2), .A2(C17_s1), .S3(C18_s3), .A1(C17_s0), .A0(C7_s3), .S2(C18_s2), .S1(C18_s1), .S0(C18_s0));
  ADD3 C26 (.A3(C25_s2), .A2(C25_s1), .S3(C26_s3), .A1(C25_s0), .A0(C18_s3), .S2(C26_s2), .S1(C26_s1), .S0(C26_s0));
  ADD3 C27 (.A3(C26_s2), .A2(C26_s1), .S3(C27_s3), .A1(C26_s0), .A0(C19_s3), .S2(C27_s2), .S1(C27_s1), .S0(C27_s0));
  ADD3 C28 (.A3(C27_s2), .A2(C27_s1), .S3(C28_s3), .A1(C27_s0), .A0(C20_s3), .S2(C28_s2), .S1(C28_s1), .S0(C28_s0));
  ADD3 C29 (.A3(C28_s2), .A2(C28_s1), .S3(C29_s3), .A1(C28_s0), .A0(C21_s3), .S2(C29_s2), .S1(C29_s1), .S0(C29_s0));
  ADD3 C34 (
    .A3(C33_s2), .A2(C33_s1), .S3(OUT10K[0]), .A1(C33_s0), .A0(C29_s3), .S2(OUT1K[3]), .S1(OUT1K[2]),
    .S0(OUT1K[1]));
  ADD3 C5 (
    .A3(C4_s2), .A2(C4_s1), .S3(C5_s3), .A1(C4_s0), .A0(multiplexer_1_out[9]), .S2(C5_s2), .S1(C5_s1),
    .S0(C5_s0));
  ADD3 C6 (
    .A3(C5_s2), .A2(C5_s1), .S3(C6_s3), .A1(C5_s0), .A0(multiplexer_1_out[8]), .S2(C6_s2), .S1(C6_s1),
    .S0(C6_s0));
  ADD3 C7 (
    .A3(C6_s2), .A2(C6_s1), .S3(C7_s3), .A1(C6_s0), .A0(multiplexer_1_out[7]), .S2(C7_s2), .S1(C7_s1),
    .S0(C7_s0));
  ADD3 C8 (
    .A3(C7_s2), .A2(C7_s1), .S3(C8_s3), .A1(C7_s0), .A0(multiplexer_1_out[6]), .S2(C8_s2), .S1(C8_s1),
    .S0(C8_s0));
  ADD3 C19 (.A3(C18_s2), .A2(C18_s1), .S3(C19_s3), .A1(C18_s0), .A0(C8_s3), .S2(C19_s2), .S1(C19_s1), .S0(C19_s0));
  ADD3 C20 (.A3(C19_s2), .A2(C19_s1), .S3(C20_s3), .A1(C19_s0), .A0(C9_s3), .S2(C20_s2), .S1(C20_s1), .S0(C20_s0));
  ADD3 C21 (.A3(C20_s2), .A2(C20_s1), .S3(C21_s3), .A1(C20_s0), .A0(C10_s3), .S2(C21_s2), .S1(C21_s1), .S0(C21_s0));
  ADD3 C22 (.A3(C21_s2), .A2(C21_s1), .S3(C22_s3), .A1(C21_s0), .A0(C11_s3), .S2(C22_s2), .S1(C22_s1), .S0(C22_s0));
  ADD3 C30 (
    .A3(C29_s2), .A2(C29_s1), .S3(OUT1K[0]), .A1(C29_s0), .A0(C22_s3), .S2(OUT100[3]), .S1(OUT100[2]),
    .S0(OUT100[1]));
  ADD3 C9 (
    .A3(C8_s2), .A2(C8_s1), .S3(C9_s3), .A1(C8_s0), .A0(multiplexer_1_out[5]), .S2(C9_s2), .S1(C9_s1),
    .S0(C9_s0));
  ADD3 C10 (
    .A3(C9_s2), .A2(C9_s1), .S3(C10_s3), .A1(C9_s0), .A0(multiplexer_1_out[4]), .S2(C10_s2), .S1(C10_s1),
    .S0(C10_s0));
  ADD3 C11 (
    .A3(C10_s2), .A2(C10_s1), .S3(C11_s3), .A1(C10_s0), .A0(multiplexer_1_out[3]), .S2(C11_s2), .S1(C11_s1),
    .S0(C11_s0));
  ADD3 C12 (
    .A3(C11_s2), .A2(C11_s1), .S3(C12_s3), .A1(C11_s0), .A0(multiplexer_1_out[2]), .S2(C12_s2), .S1(C12_s1),
    .S0(C12_s0));
  ADD3 C23 (
    .A3(C22_s2), .A2(C22_s1), .S3(OUT100[0]), .A1(C22_s0), .A0(C12_s3), .S2(OUT10[3]), .S1(OUT10[2]),
    .S0(OUT10[1]));
  ADD3 C13 (
    .A3(C12_s2), .A2(C12_s1), .S3(OUT10[0]), .A1(C12_s0), .A0(multiplexer_1_out[1]), .S2(OUT1[3]),
    .S1(OUT1[2]), .S0(OUT1[1]));

  assign SGN = IN[15];
endmodule

module ADD3 (
  input  A3,
  input  A2,
  input  A1,
  input  A0,
  output S3,
  output S2,
  output S1,
  output S0
);

  wire and_1_out, and_2_out, and_3_out, and_4_out, and_5_out, and_6_out, and_7_out, and_8_out, and_9_out,
       and_10_out, and_11_out, and_12_out, and_13_out, not_1_out, not_2_out, not_3_out, not_4_out, not_5_out,
       not_6_out, not_7_out, not_8_out;

  and and_1 (and_1_out, A2, A0);
  and and_2 (and_2_out, A2, A1);
  and and_3 (and_3_out, A2, not_1_out, not_2_out);
  not not_1 (not_1_out, A1);
  not not_2 (not_2_out, A0);
  and and_4 (and_4_out, A3, A0);
  and and_5 (and_5_out, A3, A1);
  not not_3 (not_3_out, A2);
  and and_6 (and_6_out, not_3_out, A1);
  and and_7 (and_7_out, A1, A0);
  and and_8 (and_8_out, A3, not_4_out);
  not not_4 (not_4_out, A0);
  and and_9 (and_9_out, A3, A2);
  not not_5 (not_5_out, A3);
  not not_6 (not_6_out, A2);
  and and_10 (and_10_out, not_5_out, not_6_out, A0);
  and and_11 (and_11_out, A2, A1, not_7_out);
  not not_7 (not_7_out, A0);
  and and_12 (and_12_out, A3, not_8_out);
  not not_8 (not_8_out, A0);
  and and_13 (and_13_out, A3, A1);
  or or_1 (S3, and_1_out, and_2_out, A3);
  or or_2 (S2, and_3_out, and_4_out, and_5_out);
  or or_3 (S1, and_6_out, and_7_out, and_8_out, and_9_out);
  or or_4 (S0, and_10_out, and_11_out, and_12_out, and_13_out);
endmodule

// 00
module _00_LastNumberEnteredFromDigitButtons (
  input  [15:0] pressed,
  input  clickhappens,
  input  [3:0] cPressed,
  input  CLR,
  input  DEL,
  input  NEG,
  input  CLK,
  output [15:0] out_8,
  output OVF
);

  wire adder_1_cout, adder_2_cout, adder_3_cout, adder_4_cout;
  wire [15:0] adder_1_out, adder_2_out, adder_3_out, adder_4_out, multiplexer_1_out, negator_1_out,
       register_1_q, register_2_q, register_3_q, register_4_q, register_5_q, x10_1_out_2, x10_2_out_2,
       x10_3_out_2, x10_4_out_2;

  x10 x10_1 (.in_1(register_2_q), .out_2(x10_1_out_2));
  x10 x10_2 (.in_1(register_3_q), .out_2(x10_2_out_2));
  x10 x10_3 (.in_1(register_4_q), .out_2(x10_3_out_2));
  x10 x10_4 (.in_1(register_5_q), .out_2(x10_4_out_2));
  Register #(.width(16)) register_1 (.D(x10_1_out_2), .en(clickhappens), .Q(register_1_q), .clk(CLK), .clr(CLR));
  Register #(.width(16)) register_2 (.D(x10_2_out_2), .en(clickhappens), .Q(register_2_q), .clk(CLK), .clr(CLR));
  Register #(.width(16)) register_3 (.D(x10_3_out_2), .en(clickhappens), .Q(register_3_q), .clk(CLK), .clr(CLR));
  Register #(.width(16)) register_4 (.D(x10_4_out_2), .en(clickhappens), .Q(register_4_q), .clk(CLK), .clr(CLR));
  Register #(.width(16)) register_5 (.D(pressed), .en(clickhappens), .Q(register_5_q), .clk(CLK), .clr(CLR));
  Adder #(.width(16)) adder_1 (.a(register_1_q), .b(adder_2_out), .out(adder_1_out), .cout(adder_1_cout));  // open: cin
  Adder #(.width(16)) adder_2 (.a(register_2_q), .b(adder_3_out), .out(adder_2_out), .cout(adder_2_cout));  // open: cin
  Adder #(.width(16)) adder_3 (.a(register_3_q), .b(adder_4_out), .out(adder_3_out), .cout(adder_3_cout));  // open: cin
  Adder #(.width(16)) adder_4 (
    .a(register_4_q), .b(register_5_q), .out(adder_4_out), .cout(adder_4_cout));  // open: cin
  or or_1 (OVF, adder_4_cout, adder_3_cout, adder_2_cout, adder_1_cout);
  Multiplexer #(.select(4), .width(16)) multiplexer_1 (
    .in0({16{1'b0}}), .in1(register_5_q), .in2(adder_4_out), .in3(adder_3_out), .in4(adder_2_out),
    .in5(adder_1_out), .in6({16{1'b0}}), .in7({16{1'b0}}), .in8({16{1'b0}}), .in9({16{1'b0}}),
    .in10({16{1'b0}}), .in11({16{1'b0}}), .in12({16{1'b0}}), .in13({16{1'b0}}), .in14({16{1'b0}}),
    .in15({16{1'b0}}), .out(multiplexer_1_out), .sel(cPressed));  // open: en
  Negator #(.width(16)) negator_1 (.in(multiplexer_1_out), .out(negator_1_out));
  Multiplexer #(.width(16)) multiplexer_2 (
    .in0(multiplexer_1_out), .in1(negator_1_out), .out(out_8), .sel(NEG));  // open: en
endmodule

// 01
module _01_DataPathController (
  input  [15:0] in_1,
  input  [3:0] trueopcode,
  input  [1:0] recallwhere,
  input  [1:0] storewhere,
  input  d,
  input  in_6,
  input  CLK,
  output [15:0] out_8,
  output OPmode,
  output SRmode,
  output out_11
);

  wire and_1_out, nand_1_out, nor_1_out, or_1_out, or_2_out, or_3_out;
  wire [3:0] multiplexer_1_out, multiplexer_2_out, multiplexer_3_out, multiplexer_4_out, multiplexer_5_out;
  wire [15:0] datapath_1_dout, ram_1_data;

  and and_1 (and_1_out, OPmode, nand_1_out);
  nand nand_1 (nand_1_out, trueopcode[0], trueopcode[1], trueopcode[2], trueopcode[3]);
  nor nor_1 (nor_1_out, recallwhere[0], recallwhere[1]);
  or or_1 (or_1_out, recallwhere[0], recallwhere[1]);
  Multiplexer #(.width(4)) multiplexer_1 (
    .in0({2'b00, recallwhere}), .in1(4'b1111), .out(multiplexer_1_out), .sel(nor_1_out));  // open: en
  Multiplexer #(.width(4)) multiplexer_2 (
    .in0(4'b0010), .in1(trueopcode), .out(multiplexer_2_out), .sel(nand_1_out));  // open: en
  Multiplexer #(.width(4)) multiplexer_3 (
    .in0(4'b0000), .in1(4'b0001), .out(multiplexer_3_out), .sel(nand_1_out));  // open: en
  Multiplexer #(.width(4)) multiplexer_4 (
    .in0(multiplexer_1_out), .in1(4'b1111), .out(multiplexer_4_out), .sel(nand_1_out));  // open: en
  or or_2 (or_2_out, storewhere[0], storewhere[1]);
  Multiplexer #(.width(4)) multiplexer_5 (
    .in0({2'b00, storewhere}), .in1(4'b1010), .out(multiplexer_5_out), .sel(nand_1_out));  // open: en
  DATAPATH datapath_1 (
    .DIN(in_1), .INSTR({multiplexer_2_out, multiplexer_3_out, multiplexer_4_out, multiplexer_5_out}),
    .CLK(CLK), .DOUT(datapath_1_dout), .FOVF(out_11));  // open: FZERO, FNEG
  ClickThenStayOnTillReset clickthenstayontillreset_1 (
    .buttontapped(nand_1_out), .reset(or_3_out), .clk(CLK), .buttonon(OPmode));
  or or_3 (or_3_out, d, in_6, SRmode);
  or or_4 (SRmode, or_2_out, or_1_out);
  RAM #(.addrWidth(2), .dataWidth(16), .bus("separate")) ram_1 (
    .addr(2'b00), .din(datapath_1_dout), .data(ram_1_data), .str(nand_1_out), .clk(CLK));  // open: sel, ld, clr
  Multiplexer #(.width(16)) multiplexer_6 (
    .in0(datapath_1_dout), .in1(ram_1_data), .out(out_8), .sel(OPmode));  // open: en
endmodule

// #Tap
module CountPressed (
  input  numberpressed,
  input  deletepressed,
  input  cError,
  input  CLK,
  output [3:0] amountpressed,
  output ERR
);

  wire and_1_out, nZero;
  wire [15:0] adder_1_out, bit_extender_1_out, bit_extender_2_out, ButtonsPressed_q, subtractor_1_out;

  assign bit_extender_1_out = {{15{1'b0}}, numberpressed};  // Bit_Extender bit_extender_1
  and and_1 (and_1_out, deletepressed, nZero);
  or or_1 (nZero, adder_1_out[15], adder_1_out[14], adder_1_out[13], adder_1_out[12], adder_1_out[11], adder_1_out[10], adder_1_out[9], adder_1_out[8], adder_1_out[7], adder_1_out[6], adder_1_out[5], adder_1_out[4], adder_1_out[3], adder_1_out[2], adder_1_out[1], adder_1_out[0]);
  Adder #(.width(16)) adder_1 (.a(ButtonsPressed_q), .b(bit_extender_1_out), .out(adder_1_out));  // open: cin, cout
  assign bit_extender_2_out = {{15{1'b0}}, and_1_out};  // Bit_Extender bit_extender_2
  Register #(.width(16)) ButtonsPressed (
    .D(subtractor_1_out), .Q(ButtonsPressed_q), .clk(CLK), .clr(cError));  // open: en
  Subtractor #(.width(16)) subtractor_1 (
    .a(adder_1_out), .b(bit_extender_2_out), .out(subtractor_1_out));  // open: bin, bout
  Bit_Extender #(.in_width(16), .out_width(4)) bit_extender_3 (.in(ButtonsPressed_q), .out(amountpressed));
  Hex_Digit_Display hex_digit_display_1 (.value(amountpressed));  // open: dp
  Comparator #(.width(16)) comparator_1 (.a(ButtonsPressed_q), .b(16'h4), .gt(ERR));  // open: eq, lt
endmodule

// Tap
module ClickOneHigh (
  input  press,
  input  CLK,
  output ispressed
);

  wire and_1_out, and_2_out, and_3_out, d_ff_1_q, not_1_out, not_2_out, or_1_out;

  and and_1 (and_1_out, ispressed, press);
  and and_2 (and_2_out, d_ff_1_q, press);
  not not_1 (not_1_out, d_ff_1_q);
  not not_2 (not_2_out, ispressed);
  or or_1 (or_1_out, and_1_out, and_2_out);
  and and_3 (and_3_out, not_1_out, not_2_out, press);
  D_Flip_Flop d_ff_1 (.clk(CLK), .D(or_1_out), .Q(d_ff_1_q));  // open: Qn, preset, en, reset
  D_Flip_Flop d_ff_2 (.clk(CLK), .D(and_3_out), .Q(ispressed));  // open: Qn, preset, en, reset
endmodule

// Digit
module ClickValueOfDigitClicked (
  input  [9:0] Clicked_Operation,
  input  CLK,
  output [15:0] out_3,
  output clickhappens
);

  wire not_1_out, or_1_out, or_2_out, priority_encoder_1_en_out;
  wire [3:0] multiplexer_1_out, priority_encoder_1_out;
  wire [9:0] register_1_q, register_2_q, register_3_q;

  Register #(.width(10)) register_1 (.D(Clicked_Operation), .Q(register_1_q), .clk(CLK));  // open: en, clr
  or or_1 (or_1_out, Clicked_Operation[0], Clicked_Operation[1], Clicked_Operation[2], Clicked_Operation[3], Clicked_Operation[4], Clicked_Operation[5], Clicked_Operation[6], Clicked_Operation[7], Clicked_Operation[8], Clicked_Operation[9], 1'b0);
  not not_1 (not_1_out, or_1_out);
  Register #(.width(10)) register_2 (.D(register_1_q), .Q(register_2_q), .clk(not_1_out), .clr(or_2_out));  // open: en
  or or_2 (or_2_out, 1'b0, register_3_q[0], register_3_q[1], register_3_q[2], register_3_q[3], register_3_q[4], register_3_q[5], register_3_q[6], register_3_q[7], register_3_q[8], register_3_q[9]);
  Register #(.width(10)) register_3 (.D(register_2_q), .Q(register_3_q), .clk(CLK));  // open: en, clr
  or or_3 (clickhappens, 1'b0, register_2_q[0], register_2_q[1], register_2_q[2], register_2_q[3], register_2_q[4], register_2_q[5], register_2_q[6], register_2_q[7], register_2_q[8], register_2_q[9]);
  Priority_Encoder #(.select(4), .disabled(0)) priority_encoder_1 (
    .in0(register_2_q[0]), .in1(register_2_q[1]), .in2(register_2_q[2]), .in3(register_2_q[3]),
    .in4(register_2_q[4]), .in5(register_2_q[5]), .in6(register_2_q[6]), .in7(register_2_q[7]),
    .in8(register_2_q[8]), .in9(register_2_q[9]), .out(priority_encoder_1_out),
    .en_out(priority_encoder_1_en_out));  // open: in10, in11, in12, in13, in14, in15, gs, en_in
  Multiplexer #(.width(4)) multiplexer_1 (
    .in0(priority_encoder_1_out), .in1(4'b0000), .out(multiplexer_1_out), .sel(priority_encoder_1_en_out));  // open: en
  assign out_3 = {{12{1'b0}}, multiplexer_1_out};  // Bit_Extender bit_extender_1
endmodule

// 11
module ClickOperation (
  input  [15:0] Clicked_Operation,
  input  CLK,
  output [3:0] OPCODE,
  output clickhappens
);

  wire nor_1_out, not_1_out, or_1_out, or_2_out, or_4_out;
  wire [15:0] register_1_q, register_2_q, register_3_q;

  Register #(.width(16)) register_1 (.D(Clicked_Operation), .Q(register_1_q), .clk(CLK));  // open: en, clr
  or or_1 (or_1_out, 1'b0, Clicked_Operation[0], Clicked_Operation[1], Clicked_Operation[2], Clicked_Operation[3], Clicked_Operation[4], Clicked_Operation[5], Clicked_Operation[6], Clicked_Operation[7], Clicked_Operation[8], Clicked_Operation[9], Clicked_Operation[10], Clicked_Operation[11], Clicked_Operation[12], Clicked_Operation[13], Clicked_Operation[14], Clicked_Operation[15]);
  not not_1 (not_1_out, or_1_out);
  Register #(.width(16)) register_2 (.D(register_1_q), .Q(register_2_q), .clk(not_1_out), .clr(or_2_out));  // open: en
  Register #(.width(16)) register_3 (.D(register_2_q), .Q(register_3_q), .clk(CLK));  // open: en, clr
  or or_2 (or_2_out, register_3_q[0], register_3_q[1], register_3_q[2], register_3_q[3], register_3_q[4], register_3_q[5], register_3_q[6], register_3_q[7], register_3_q[8], register_3_q[9], register_3_q[10], register_3_q[11], register_3_q[12], register_3_q[13], register_3_q[14], register_3_q[15], 1'b0);
  nor nor_1 (nor_1_out, register_2_q[0], register_2_q[1], register_2_q[2], register_2_q[3], register_2_q[4], register_2_q[5], register_2_q[6], register_2_q[7], register_2_q[8], register_2_q[9], register_2_q[10], register_2_q[11], register_2_q[12], register_2_q[13], register_2_q[14], register_2_q[15], 1'b0);
  or or_3 (clickhappens, 1'b0, register_2_q[0], register_2_q[1], register_2_q[2], register_2_q[3], register_2_q[4], register_2_q[5], register_2_q[6], register_2_q[8], register_2_q[9], register_2_q[10], register_2_q[11], register_2_q[12], register_2_q[13], register_2_q[14], register_2_q[15]);
  or or_4 (or_4_out, register_2_q[15], nor_1_out);
  Priority_Encoder #(.select(4)) priority_encoder_1 (
    .in0(register_2_q[0]), .in1(register_2_q[1]), .in2(register_2_q[2]), .in3(register_2_q[3]),
    .in4(register_2_q[4]), .in5(register_2_q[5]), .in6(register_2_q[6]), .in7(register_2_q[7]),
    .in8(register_2_q[8]), .in9(register_2_q[9]), .in10(register_2_q[10]), .in11(register_2_q[11]),
    .in12(register_2_q[12]), .in13(register_2_q[13]), .in14(register_2_q[14]), .in15(or_4_out), .out(OPCODE));  // open: gs, en_out, en_in
endmodule

module ClickThenStayOnTillReset (
  input  buttontapped,
  input  reset,
  input  clk,
  output buttonon
);

  wire and_1_out, and_2_out, and_3_out, and_4_out, d_ff_1_q, not_1_out, not_2_out, not_3_out, not_4_out,
       or_2_out;

  not not_1 (not_1_out, reset);
  not not_2 (not_2_out, reset);
  not not_3 (not_3_out, reset);
  not not_4 (not_4_out, reset);
  and and_1 (and_1_out, not_1_out, d_ff_1_q);
  or or_1 (buttonon, and_1_out, and_2_out);
  and and_2 (and_2_out, buttontapped, not_2_out);
  and and_3 (and_3_out, not_3_out, d_ff_1_q);
  or or_2 (or_2_out, and_3_out, and_4_out);
  and and_4 (and_4_out, buttontapped, not_4_out);
  D_Flip_Flop d_ff_1 (.clk(clk), .D(or_2_out), .Q(d_ff_1_q));  // open: Qn, preset, en, reset
endmodule

module ClickHolder (
  input  [2:0] in_1,
  input  RST,
  input  CLK,
  output [2:0] Operation_Clicked
);

  wire not_1_out, or_1_out;
  wire [2:0] register_1_q;

  Register #(.width(3)) register_1 (.D(in_1), .Q(register_1_q), .clk(CLK));  // open: en, clr
  or or_1 (or_1_out, in_1[0], in_1[1], in_1[2]);
  not not_1 (not_1_out, or_1_out);
  Register #(.width(3)) register_2 (.D(register_1_q), .Q(Operation_Clicked), .clk(not_1_out), .clr(RST));  // open: en
endmodule

// Toggle
module ClickToggleForMinusButton (
  input  in_1,
  input  CLK,
  input  in_3,
  output out_4
);

  wire and_1_out, d_ff_1_q, multiplexer_1_out, not_1_out, not_2_out;

  and and_1 (and_1_out, out_4, in_1);
  not not_1 (not_1_out, in_1);
  Multiplexer multiplexer_1 (.in0(in_1), .in1(not_1_out), .out(multiplexer_1_out), .sel(and_1_out));  // open: en
  D_Flip_Flop d_ff_1 (.clk(CLK), .D(multiplexer_1_out), .Q(d_ff_1_q));  // open: Qn, preset, en, reset
  D_Flip_Flop d_ff_2 (.clk(not_2_out), .D(d_ff_1_q), .Q(out_4), .reset(in_3));  // open: Qn, preset, en
  not not_2 (not_2_out, in_1);
endmodule

module ClickNHold (
  input  in_1,
  input  CLK,
  input  in_3,
  output out_4
);

  wire d_ff_1_q, not_1_out, or_1_out;

  D_Flip_Flop d_ff_1 (.clk(CLK), .D(in_1), .Q(d_ff_1_q));  // open: Qn, preset, en, reset
  or or_1 (or_1_out, out_4, d_ff_1_q);
  D_Flip_Flop d_ff_2 (.clk(not_1_out), .D(or_1_out), .Q(out_4), .reset(in_3));  // open: Qn, preset, en
  not not_1 (not_1_out, in_1);
endmodule

module ClickStoreRecallButtonProcessor (
  input  [2:0] in_1,
  input  stopsr,
  input  CLK,
  output [1:0] out_4,
  output amsr
);

  wire clicknhold_1_out_4, clicknhold_2_out_4, clicknhold_3_out_4, or_2_out, or_3_out, or_4_out;

  or or_1 (amsr, in_1[2], in_1[1], in_1[0]);
  // AND_Gate and_1 is placed but not wired
  ClickNHold clicknhold_1 (.in_1(in_1[0]), .CLK(CLK), .in_3(or_4_out), .out_4(clicknhold_1_out_4));
  ClickNHold clicknhold_2 (.in_1(in_1[1]), .CLK(CLK), .in_3(or_2_out), .out_4(clicknhold_2_out_4));
  ClickNHold clicknhold_3 (.in_1(in_1[2]), .CLK(CLK), .in_3(or_3_out), .out_4(clicknhold_3_out_4));
  or or_2 (or_2_out, in_1[2], stopsr, in_1[0]);
  or or_3 (or_3_out, in_1[1], stopsr, in_1[0]);
  Priority_Encoder #(.select(2), .disabled(0)) priority_encoder_1 (
    .in0(1'b1), .in1(clicknhold_1_out_4), .in2(clicknhold_2_out_4), .in3(clicknhold_3_out_4), .out(out_4));  // open: gs, en_out, en_in
  or or_4 (or_4_out, in_1[2], stopsr, in_1[1]);
endmodule

module ClickUntilreset (
  input  in_1,
  input  RST,
  input  CLK,
  output out_4
);

  wire not_1_out, register_1_q;

  Register #(.width(1)) register_1 (.D(in_1), .Q(register_1_q), .clk(CLK));  // open: en, clr
  not not_1 (not_1_out, in_1);
  Register #(.width(1)) register_2 (.D(register_1_q), .Q(out_4), .clk(not_1_out), .clr(RST));  // open: en
endmodule

module Clickcrazy (
  input  in_1,
  input  CLK,
  output out_3
);

  wire and_1_out, d_ff_1_q, not_1_out;

  not not_1 (not_1_out, in_1);
  D_Flip_Flop d_ff_1 (.clk(CLK), .D(in_1), .Q(d_ff_1_q), .reset(and_1_out));  // open: Qn, preset, en
  and and_1 (and_1_out, out_3, in_1);
  D_Flip_Flop d_ff_2 (.clk(not_1_out), .D(d_ff_1_q), .Q(out_3), .reset(and_1_out));  // open: Qn, preset, en
endmodule

// Display
module DisplayMain (
  input  [15:0] IN,
  input  [1:0] DisplayMode,
  output SGN,
  output [6:0] SSD4,
  output [6:0] SSD3,
  output [6:0] SSD2,
  output [6:0] SSD1,
  output [6:0] SSD0
);

  wire DECSGN, ErrorSGN, HEXSGN, TWCSGN;
  wire [6:0] DEC0, DEC1, DEC2, DEC3, DEC4, Error0, Error1, Error2, Error3, Error4, HEX0, HEX1, HEX2, HEX3,
       HEX4, SSD0_t, SSD1_t, SSD2_t, SSD3_t, SSD4_t, TWC0, TWC1, TWC2, TWC3, TWC4;

  DisplayTWC displaytwc_1 (
    .MyNumber(IN), .SGN(TWCSGN), .SSD4(TWC4), .SSD3(TWC3), .SSD2(TWC2), .SSD1(TWC1), .SSD0(TWC0));
  DisplayHex displayhex_1 (
    .MyNumber(IN), .SGN(HEXSGN), .SSD4(HEX4), .SSD3(HEX3), .SSD2(HEX2), .SSD1(HEX1), .SSD0(HEX0));
  DisplayDecimal displaydecimal_1 (
    .MyNumber(IN), .SGN(DECSGN), .SSD4(DEC4), .SSD3(DEC3), .SSD2(DEC2), .SSD1(DEC1), .SSD0(DEC0));
  DisplayError displayerror_1 (
    .SGN(ErrorSGN), .SSD4(Error4), .SSD3(Error3), .SSD2(Error2), .SSD1(Error1), .SSD0(Error0));
  Multiplexer #(.select(2)) multiplexer_1 (
    .in0(DECSGN), .in1(HEXSGN), .in2(TWCSGN), .in3(ErrorSGN), .out(SGN), .sel(DisplayMode));  // open: en
  Multiplexer #(.select(2), .width(7)) multiplexer_2 (
    .in0(DEC4), .in1(HEX4), .in2(TWC4), .in3(Error4), .out(SSD4_t), .sel(DisplayMode));  // open: en
  Multiplexer #(.select(2), .width(7)) multiplexer_3 (
    .in0(DEC3), .in1(HEX3), .in2(TWC3), .in3(Error3), .out(SSD3_t), .sel(DisplayMode));  // open: en
  Multiplexer #(.select(2), .width(7)) multiplexer_4 (
    .in0(DEC2), .in1(HEX2), .in2(TWC2), .in3(Error2), .out(SSD2_t), .sel(DisplayMode));  // open: en
  Multiplexer #(.select(2), .width(7)) multiplexer_5 (
    .in0(DEC1), .in1(HEX1), .in2(TWC1), .in3(Error1), .out(SSD1_t), .sel(DisplayMode));  // open: en
  Multiplexer #(.select(2), .width(7)) multiplexer_6 (
    .in0(DEC0), .in1(HEX0), .in2(TWC0), .in3(Error0), .out(SSD0_t), .sel(DisplayMode));  // open: en
  DisplayRewiring displayrewiring_1 (.in_1(SSD4_t), .out_2(SSD4));
  DisplayRewiring displayrewiring_2 (.in_1(SSD3_t), .out_2(SSD3));
  DisplayRewiring displayrewiring_3 (.in_1(SSD2_t), .out_2(SSD2));
  DisplayRewiring displayrewiring_4 (.in_1(SSD1_t), .out_2(SSD1));
  DisplayRewiring displayrewiring_5 (.in_1(SSD0_t), .out_2(SSD0));
endmodule

// 11.1
module _11_1_DisplayMode (
  input  DEC,
  input  HEX,
  input  TWC,
  input  ERROR,
  input  CLK,
  output [1:0] out_6
);

  wire or_1_out, or_2_out, or_3_out, or_4_out, s_r_ff_1_q, s_r_ff_2_q, s_r_ff_3_q, s_r_ff_4_q;

  or or_1 (or_1_out, HEX, TWC, ERROR);
  or or_2 (or_2_out, DEC, TWC, ERROR);
  or or_3 (or_3_out, DEC, HEX, ERROR);
  or or_4 (or_4_out, DEC, HEX, TWC);
  S_R_Flip_Flop s_r_ff_1 (.S(DEC), .clk(CLK), .R(or_1_out), .Q(s_r_ff_1_q));  // open: Qn, preset, reset, en
  S_R_Flip_Flop s_r_ff_2 (.S(HEX), .clk(CLK), .R(or_2_out), .Q(s_r_ff_2_q));  // open: Qn, preset, reset, en
  S_R_Flip_Flop s_r_ff_3 (.S(TWC), .clk(CLK), .R(or_3_out), .Q(s_r_ff_3_q));  // open: Qn, preset, reset, en
  S_R_Flip_Flop s_r_ff_4 (.S(ERROR), .clk(CLK), .R(or_4_out), .Q(s_r_ff_4_q));  // open: Qn, preset, reset, en
  Priority_Encoder #(.select(2), .disabled(0)) priority_encoder_1 (
    .in0(s_r_ff_1_q), .in1(s_r_ff_2_q), .in2(s_r_ff_3_q), .in3(s_r_ff_4_q), .out(out_6));  // open: gs, en_out, en_in
endmodule

// Error
module DisplayError (
  output SGN,
  output [6:0] SSD4,
  output [6:0] SSD3,
  output [6:0] SSD2,
  output [6:0] SSD1,
  output [6:0] SSD0
);

  _7_Segment_Display u_7_segment_display_1 (
    .g(1'b1), .f(1'b1), .a(1'b1), .b(1'b0), .e(1'b1), .d(1'b1), .c(1'b0), .dp(1'b0));
  _7_Segment_Display u_7_segment_display_2 (
    .g(1'b1), .f(1'b0), .a(1'b0), .b(1'b0), .e(1'b1), .d(1'b0), .c(1'b0), .dp(1'b0));
  _7_Segment_Display u_7_segment_display_3 (
    .g(1'b1), .f(1'b0), .a(1'b0), .b(1'b0), .e(1'b1), .d(1'b0), .c(1'b0), .dp(1'b0));
  _7_Segment_Display u_7_segment_display_4 (
    .g(1'b1), .f(1'b0), .a(1'b0), .b(1'b0), .e(1'b1), .d(1'b1), .c(1'b1));  // open: dp
  _7_Segment_Display u_7_segment_display_5 (
    .g(1'b1), .f(1'b0), .a(1'b0), .b(1'b0), .e(1'b1), .d(1'b0), .c(1'b0), .dp(1'b0));

  assign SGN = 1'b0;
  assign SSD0 = 7'b0000101;
  assign SSD1 = 7'b0011101;
  assign SSD2 = 7'b0000101;
  assign SSD3 = 7'b0000101;
  assign SSD4 = 7'b1001111;
endmodule

// Digit
module DisplayDigit (
  input  [3:0] BCD,
  output _0,
  output _1,
  output _2,
  output _5,
  output _4,
  output _3,
  output _6
);

  wire _0_t, _1_t, _2_t, _3_t, _4_t, _5_t, _6_t, _7, _8, _9, A, B, C, D, E, F;

  Decoder #(.select(4)) decoder_1 (
    .out0(_0_t), .out1(_1_t), .out2(_2_t), .out3(_3_t), .out4(_4_t), .out5(_5_t), .out6(_6_t), .out7(_7),
    .out8(_8), .out9(_9), .out10(A), .out11(B), .out12(C), .out13(D), .out14(E), .out15(F), .sel(BCD));  // open: en
  _7_Segment_Display u_7_segment_display_1 (.g(_0), .f(_1), .a(_6), .b(_5), .e(_2), .d(_3), .c(_4));  // open: dp
  or or_1 (_1, _0_t, _4_t, _5_t, _6_t, _8, _9, A, B, C, E, F);
  or or_2 (_3, _0_t, _2_t, _3_t, _5_t, _6_t, _8, _9, B, C, D, E);
  or or_3 (_0, _2_t, _3_t, _4_t, _5_t, _6_t, _8, _9, A, B, D, E, F);
  or or_4 (_4, _0_t, _1_t, _3_t, _4_t, _5_t, _6_t, _7, _8, _9, A, B, D);
  or or_5 (_2, _0_t, _2_t, _6_t, _8, A, B, C, D, E, F);
  or or_6 (_5, _0_t, _1_t, _2_t, _3_t, _4_t, _7, _8, _9, A, D);
  or or_7 (_6, _0_t, _2_t, _3_t, _5_t, _6_t, _7, _8, _9, A, C, E, F);

  // Other names for the same wires on the sheet: T0 = _0; T1 = _1; T2 = _2; T3 = _3; T4 = _4; T5 = _5; T6 = _6
endmodule

// DEC
module DisplayDecimal (
  input  [15:0] MyNumber,
  output SGN,
  output [6:0] SSD4,
  output [6:0] SSD3,
  output [6:0] SSD2,
  output [6:0] SSD1,
  output [6:0] SSD0
);

  wire [3:0] binary16tobcd5_1_out1, binary16tobcd5_1_out1k, binary16tobcd5_1_out10, binary16tobcd5_1_out10k,
       binary16tobcd5_1_out100;

  Binary16toBCD5 binary16tobcd5_1 (
    .IN(MyNumber), .SGN(SGN), .OUT10K(binary16tobcd5_1_out10k), .OUT1K(binary16tobcd5_1_out1k),
    .OUT100(binary16tobcd5_1_out100), .OUT10(binary16tobcd5_1_out10), .OUT1(binary16tobcd5_1_out1));
  DisplayDigit _0 (
    .BCD(binary16tobcd5_1_out1), ._0(SSD0[0]), ._1(SSD0[1]), ._2(SSD0[2]), ._5(SSD0[5]), ._4(SSD0[4]),
    ._3(SSD0[3]), ._6(SSD0[6]));
  _7_Segment_Display u_7_segment_display_1 (
    .g(SSD4[0]), .f(SSD4[1]), .a(SSD4[6]), .b(SSD4[5]), .e(SSD4[2]), .d(SSD4[3]), .c(SSD4[4]));  // open: dp
  DisplayDigit _0_2 (
    .BCD(binary16tobcd5_1_out10), ._0(SSD1[0]), ._1(SSD1[1]), ._2(SSD1[2]), ._5(SSD1[5]), ._4(SSD1[4]),
    ._3(SSD1[3]), ._6(SSD1[6]));
  _7_Segment_Display u_7_segment_display_2 (
    .g(SSD3[0]), .f(SSD3[1]), .a(SSD3[6]), .b(SSD3[5]), .e(SSD3[2]), .d(SSD3[3]), .c(SSD3[4]));  // open: dp
  _7_Segment_Display u_7_segment_display_3 (
    .g(SSD2[0]), .f(SSD2[1]), .a(SSD2[6]), .b(SSD2[5]), .e(SSD2[2]), .d(SSD2[3]), .c(SSD2[4]));  // open: dp
  DisplayDigit _0_3 (
    .BCD(binary16tobcd5_1_out100), ._0(SSD2[0]), ._1(SSD2[1]), ._2(SSD2[2]), ._5(SSD2[5]), ._4(SSD2[4]),
    ._3(SSD2[3]), ._6(SSD2[6]));
  _7_Segment_Display u_7_segment_display_4 (
    .g(SSD1[0]), .f(SSD1[1]), .a(SSD1[6]), .b(SSD1[5]), .e(SSD1[2]), .d(SSD1[3]), .c(SSD1[4]));  // open: dp
  DisplayDigit _0_4 (
    .BCD(binary16tobcd5_1_out1k), ._0(SSD3[0]), ._1(SSD3[1]), ._2(SSD3[2]), ._5(SSD3[5]), ._4(SSD3[4]),
    ._3(SSD3[3]), ._6(SSD3[6]));
  _7_Segment_Display u_7_segment_display_5 (
    .g(SSD0[0]), .f(SSD0[1]), .a(SSD0[6]), .b(SSD0[5]), .e(SSD0[2]), .d(SSD0[3]), .c(SSD0[4]));  // open: dp
  DisplayDigit _0_5 (
    .BCD(binary16tobcd5_1_out10k), ._0(SSD4[0]), ._1(SSD4[1]), ._2(SSD4[2]), ._5(SSD4[5]), ._4(SSD4[4]),
    ._3(SSD4[3]), ._6(SSD4[6]));

  // Other names for the same wires on the sheet: _00 = SSD0[0]; _01 = SSD0[1]; _02 = SSD0[2]; _03 = SSD0[3];
  //   _04 = SSD0[4]; _05 = SSD0[5]; _06 = SSD0[6]; _10 = SSD1[0]; _11 = SSD1[1]; _12 = SSD1[2]; _13 = SSD1[3];
  //   _14 = SSD1[4]; _15 = SSD1[5]; _16 = SSD1[6]; _20 = SSD2[0]; _21 = SSD2[1]; _22 = SSD2[2]; _23 = SSD2[3];
  //   _24 = SSD2[4]; _25 = SSD2[5]; _26 = SSD2[6]; _30 = SSD3[0]; _31 = SSD3[1]; _32 = SSD3[2]; _33 = SSD3[3];
  //   _34 = SSD3[4]; _35 = SSD3[5]; _36 = SSD3[6]; _40 = SSD4[0]; _41 = SSD4[1]; _42 = SSD4[2]; _43 = SSD4[3];
  //   _44 = SSD4[4]; _45 = SSD4[5]; _46 = SSD4[6]
endmodule

// HEX
module DisplayHex (
  input  [15:0] MyNumber,
  output SGN,
  output [6:0] SSD4,
  output [6:0] SSD3,
  output [6:0] SSD2,
  output [6:0] SSD1,
  output [6:0] SSD0
);

  wire [3:0] multiplexer_1_out, multiplexer_2_out, multiplexer_3_out, multiplexer_4_out, n0, n1, n2, n3;

  Multiplexer #(.width(4)) multiplexer_1 (
    .in0(MyNumber[3:0]), .in1(n0), .out(multiplexer_1_out), .sel(MyNumber[15]));  // open: en
  DisplayDigit _0 (
    .BCD(multiplexer_1_out), ._0(SSD0[0]), ._1(SSD0[1]), ._2(SSD0[2]), ._5(SSD0[5]), ._4(SSD0[4]),
    ._3(SSD0[3]), ._6(SSD0[6]));
  Negator #(.width(16)) negator_1 (.in(MyNumber), .out({n3, n2, n1, n0}));
  DisplayDigit _0_2 (
    .BCD(multiplexer_2_out), ._0(SSD1[0]), ._1(SSD1[1]), ._2(SSD1[2]), ._5(SSD1[5]), ._4(SSD1[4]),
    ._3(SSD1[3]), ._6(SSD1[6]));
  Multiplexer #(.width(4)) multiplexer_2 (
    .in0(MyNumber[7:4]), .in1(n1), .out(multiplexer_2_out), .sel(MyNumber[15]));  // open: en
  _7_Segment_Display u_7_segment_display_1 (
    .g(SSD3[0]), .f(SSD3[1]), .a(SSD3[6]), .b(SSD3[5]), .e(SSD3[2]), .d(SSD3[3]), .c(SSD3[4]));  // open: dp
  Multiplexer #(.width(4)) multiplexer_3 (
    .in0(MyNumber[11:8]), .in1(n2), .out(multiplexer_3_out), .sel(MyNumber[15]));  // open: en
  _7_Segment_Display u_7_segment_display_2 (
    .g(SSD2[0]), .f(SSD2[1]), .a(SSD2[6]), .b(SSD2[5]), .e(SSD2[2]), .d(SSD2[3]), .c(SSD2[4]));  // open: dp
  DisplayDigit _0_3 (
    .BCD(multiplexer_3_out), ._0(SSD2[0]), ._1(SSD2[1]), ._2(SSD2[2]), ._5(SSD2[5]), ._4(SSD2[4]),
    ._3(SSD2[3]), ._6(SSD2[6]));
  Multiplexer #(.width(4)) multiplexer_4 (
    .in0(MyNumber[15:12]), .in1(n3), .out(multiplexer_4_out), .sel(MyNumber[15]));  // open: en
  _7_Segment_Display u_7_segment_display_3 (
    .g(SSD1[0]), .f(SSD1[1]), .a(SSD1[6]), .b(SSD1[5]), .e(SSD1[2]), .d(SSD1[3]), .c(SSD1[4]));  // open: dp
  DisplayDigit _0_4 (
    .BCD(multiplexer_4_out), ._0(SSD3[0]), ._1(SSD3[1]), ._2(SSD3[2]), ._5(SSD3[5]), ._4(SSD3[4]),
    ._3(SSD3[3]), ._6(SSD3[6]));
  _7_Segment_Display u_7_segment_display_4 (
    .g(SSD0[0]), .f(SSD0[1]), .a(SSD0[6]), .b(SSD0[5]), .e(SSD0[2]), .d(SSD0[3]), .c(SSD0[4]));  // open: dp

  assign SGN = MyNumber[15];
  assign SSD4 = {7{1'b0}};

  // Other names for the same wires on the sheet: p0[3:0] = MyNumber[3:0]; p1[3:0] = MyNumber[7:4];
  //   p2[3:0] = MyNumber[11:8]; p3[3:0] = MyNumber[15:12]; _00 = SSD0[0]; _01 = SSD0[1]; _02 = SSD0[2]; _03 = SSD0[3];
  //   _04 = SSD0[4]; _05 = SSD0[5]; _06 = SSD0[6]; _10 = SSD1[0]; _11 = SSD1[1]; _12 = SSD1[2]; _13 = SSD1[3];
  //   _14 = SSD1[4]; _15 = SSD1[5]; _16 = SSD1[6]; _20 = SSD2[0]; _21 = SSD2[1]; _22 = SSD2[2]; _23 = SSD2[3];
  //   _24 = SSD2[4]; _25 = SSD2[5]; _26 = SSD2[6]; _30 = SSD3[0]; _31 = SSD3[1]; _32 = SSD3[2]; _33 = SSD3[3];
  //   _34 = SSD3[4]; _35 = SSD3[5]; _36 = SSD3[6]
endmodule

// TWC
module DisplayTWC (
  input  [15:0] MyNumber,
  output SGN,
  output [6:0] SSD4,
  output [6:0] SSD3,
  output [6:0] SSD2,
  output [6:0] SSD1,
  output [6:0] SSD0
);

  DisplayDigit _0 (
    .BCD(MyNumber[3:0]), ._0(SSD0[0]), ._1(SSD0[1]), ._2(SSD0[2]), ._5(SSD0[5]), ._4(SSD0[4]), ._3(SSD0[3]),
    ._6(SSD0[6]));
  DisplayDigit _0_2 (
    .BCD(MyNumber[7:4]), ._0(SSD1[0]), ._1(SSD1[1]), ._2(SSD1[2]), ._5(SSD1[5]), ._4(SSD1[4]), ._3(SSD1[3]),
    ._6(SSD1[6]));
  _7_Segment_Display u_7_segment_display_1 (
    .g(SSD3[0]), .f(SSD3[1]), .a(SSD3[6]), .b(SSD3[5]), .e(SSD3[2]), .d(SSD3[3]), .c(SSD3[4]));  // open: dp
  _7_Segment_Display u_7_segment_display_2 (
    .g(SSD2[0]), .f(SSD2[1]), .a(SSD2[6]), .b(SSD2[5]), .e(SSD2[2]), .d(SSD2[3]), .c(SSD2[4]));  // open: dp
  DisplayDigit _0_3 (
    .BCD(MyNumber[11:8]), ._0(SSD2[0]), ._1(SSD2[1]), ._2(SSD2[2]), ._5(SSD2[5]), ._4(SSD2[4]), ._3(SSD2[3]),
    ._6(SSD2[6]));
  _7_Segment_Display u_7_segment_display_3 (
    .g(SSD1[0]), .f(SSD1[1]), .a(SSD1[6]), .b(SSD1[5]), .e(SSD1[2]), .d(SSD1[3]), .c(SSD1[4]));  // open: dp
  DisplayDigit _0_4 (
    .BCD(MyNumber[15:12]), ._0(SSD3[0]), ._1(SSD3[1]), ._2(SSD3[2]), ._5(SSD3[5]), ._4(SSD3[4]),
    ._3(SSD3[3]), ._6(SSD3[6]));
  _7_Segment_Display u_7_segment_display_4 (
    .g(SSD0[0]), .f(SSD0[1]), .a(SSD0[6]), .b(SSD0[5]), .e(SSD0[2]), .d(SSD0[3]), .c(SSD0[4]));  // open: dp

  assign SGN = 1'b0;
  assign SSD4 = {7{1'b0}};

  // Other names for the same wires on the sheet: p0[3:0] = MyNumber[3:0]; p1[3:0] = MyNumber[7:4];
  //   p2[3:0] = MyNumber[11:8]; p3[3:0] = MyNumber[15:12]; _00 = SSD0[0]; _01 = SSD0[1]; _02 = SSD0[2]; _03 = SSD0[3];
  //   _04 = SSD0[4]; _05 = SSD0[5]; _06 = SSD0[6]; _10 = SSD1[0]; _11 = SSD1[1]; _12 = SSD1[2]; _13 = SSD1[3];
  //   _14 = SSD1[4]; _15 = SSD1[5]; _16 = SSD1[6]; _20 = SSD2[0]; _21 = SSD2[1]; _22 = SSD2[2]; _23 = SSD2[3];
  //   _24 = SSD2[4]; _25 = SSD2[5]; _26 = SSD2[6]; _30 = SSD3[0]; _31 = SSD3[1]; _32 = SSD3[2]; _33 = SSD3[3];
  //   _34 = SSD3[4]; _35 = SSD3[5]; _36 = SSD3[6]
endmodule

// 7Out
module DisplayRewiring (
  input  [6:0] in_1,
  output [6:0] out_2
);


  assign out_2 = {in_1[4:2], in_1[0], in_1[1], in_1[6:5]};
endmodule

module x10 (
  input  [15:0] in_1,
  output [15:0] out_2
);

  wire [15:0] shifter_1_out, shifter_2_out;

  Shifter #(.width(16)) shifter_1 (.in(in_1), .\dist (4'b0011), .out(shifter_1_out));
  Shifter #(.width(16)) shifter_2 (.in(in_1), .\dist (4'b0001), .out(shifter_2_out));
  Adder #(.width(16)) adder_1 (.a(shifter_1_out), .b(shifter_2_out), .out(out_2));  // open: cin, cout
endmodule

module CheckTooBig (
  input  [15:0] in_1,
  output error
);

  wire comparator_1_gt, comparator_2_lt;

  Comparator #(.width(16)) comparator_1 (.a(in_1), .b(16'h270f), .gt(comparator_1_gt));  // open: eq, lt
  Comparator #(.width(16)) comparator_2 (.a(in_1), .b(16'hd8f1), .lt(comparator_2_lt));  // open: gt, eq
  or or_1 (error, comparator_1_gt, comparator_2_lt);
endmodule
